// Logisim project Computer.circ as structural Verilog: 25 circuits, main circuit main
module main (
);

  wire clock_1_out, clock_2_out, cpu_1_keyboard_next, cpu_1_ram_store, cpu_1_tty_clk, keyboard_1_avail;
  wire [3:0] hexdisplaysplitter_1_out_0, hexdisplaysplitter_1_out_1, hexdisplaysplitter_1_out_2,
       hexdisplaysplitter_1_out_3, hexdisplaysplitter_1_out_4, hexdisplaysplitter_1_out_5;
  wire [6:0] cpu_1_tty_data, keyboard_1_data;
  wire [7:0] cpu_1_image_index;
  wire [17:0] cpu_1_ram_address, cpu_1_ram_store_address;
  wire [22:0] cpu_1_pc;
  wire [31:0] cpu_1_ram_store_data, ram_1_data_out, rom_1_out;

  ram ram_1 (
    .Address(cpu_1_ram_address), .Store(cpu_1_ram_store), .Data_Out(ram_1_data_out),
    .StoreAddress(cpu_1_ram_store_address), .StoreData(cpu_1_ram_store_data));
  rom rom_1 (.Address_In(cpu_1_pc), .Out(rom_1_out));
  Clock clock_1 (.out(clock_1_out));
  CPU cpu_1 (
    .Rom(rom_1_out), .CLK(clock_1_out), .PC(cpu_1_pc), .Ram_Store_Address(cpu_1_ram_store_address),
    .Ram_Store(cpu_1_ram_store), .Ram_Address(cpu_1_ram_address), .Ram_Data(ram_1_data_out),
    .Ram_Store_Data(cpu_1_ram_store_data), .TTY_Data(cpu_1_tty_data), .TTY_CLK(cpu_1_tty_clk),
    .Keyboard_in(keyboard_1_data), .Keyboard_Next(cpu_1_keyboard_next), .Keyboard_Notempty(keyboard_1_avail),
    .Image_Index(cpu_1_image_index));
  Hex_Digit_Display hex_digit_display_1 (.value(hexdisplaysplitter_1_out_5));  // open: dp
  Hex_Digit_Display hex_digit_display_2 (.value(hexdisplaysplitter_1_out_4));  // open: dp
  Pull_Resistor pull_resistor_1 (.node(cpu_1_tty_data));
  TTY #(.rows(32)) tty_1 (.data(cpu_1_tty_data), .clk(cpu_1_tty_clk), .we(1'b1));  // open: clr
  Keyboard keyboard_1 (.clk(cpu_1_keyboard_next), .avail(keyboard_1_avail), .data(keyboard_1_data));  // open: re, clr
  Hex_Digit_Display hex_digit_display_3 (.value(hexdisplaysplitter_1_out_2));  // open: dp
  Hex_Digit_Display hex_digit_display_4 (.value(hexdisplaysplitter_1_out_3));  // open: dp
  Hex_Digit_Display hex_digit_display_5 (.value(hexdisplaysplitter_1_out_1));  // open: dp
  Hex_Digit_Display hex_digit_display_6 (.value(hexdisplaysplitter_1_out_0));  // open: dp
  HexDisplaySplitter hexdisplaysplitter_1 (
    .In(cpu_1_pc), .Out_0(hexdisplaysplitter_1_out_0), .Out_1(hexdisplaysplitter_1_out_1),
    .Out_2(hexdisplaysplitter_1_out_2), .Out_3(hexdisplaysplitter_1_out_3),
    .Out_4(hexdisplaysplitter_1_out_4), .Out_5(hexdisplaysplitter_1_out_5));
  Clock clock_2 (.out(clock_2_out));
  // DotMatrix #(.inputtype("select"), .matrixcols(32), .matrixrows(32), .persist(11000)) dotmatrix_1: pin names not known
  // DotMatrix #(.inputtype("select"), .matrixcols(32), .matrixrows(32), .persist(11000)) dotmatrix_2: pin names not known
  // LedMatrixDriver ledmatrixdriver_1: pin names not known; wires that end beside it: clock_2_out, cpu_1_image_index
  // DotMatrix #(.inputtype("select"), .matrixcols(32), .matrixrows(32), .persist(11000)) dotmatrix_3: pin names not known
  // DotMatrix #(.inputtype("select"), .matrixcols(32), .matrixrows(32), .persist(60)) dotmatrix_4: pin names not known

  // Notes on the sheet:
  //   PC
endmodule

module CPU (
  input  [31:0] Rom,
  input  CLK,
  input  [6:0] Keyboard_in,
  input  Keyboard_Notempty,
  output [31:0] Ram_Store_Data,
  output [17:0] Ram_Store_Address,
  output Ram_Store,
  output [17:0] Ram_Address,
  output [22:0] PC,
  output [31:0] Ram_Data,
  output [6:0] TTY_Data,
  output [7:0] Image_Index,
  output TTY_CLK,
  output Keyboard_Next
);

  wire decode_execute_1_aluenabled, decode_execute_1_clearprevious, decode_execute_1_condition_2;
  wire [3:0] decode_execute_1_alu_instructions, fetch_1_condition;
  wire [4:0] decode_execute_1_extradata, decode_execute_1_registerout, ExtraData, Register_Read_To_A,
       Register_Read_To_B, Register_Write;
  wire [17:0] decode_execute_1_ram_destination_address;
  wire [22:0] fetch_1_operands;
  wire [31:0] decode_execute_1_instruction_2, decode_execute_1_load_value, fetch_1_instruction_2, Reg_Bus_A,
       Reg_Bus_B, Status_In, Status_Register;

  register register_1 (
    .Write(Register_Write), .In(Ram_Store_Data), .OutB(Reg_Bus_B), .OutA(Reg_Bus_A),
    .ReadB(Register_Read_To_B), .ReadA(Register_Read_To_A), .My_Address({5{1'b0}}), .CLK(CLK));
  register register_2 (
    .Write(Register_Write), .In(Ram_Store_Data), .OutB(Reg_Bus_B), .OutA(Reg_Bus_A),
    .ReadB(Register_Read_To_B), .ReadA(Register_Read_To_A), .My_Address(5'b01000), .CLK(CLK));
  register register_3 (
    .Write(Register_Write), .In(Ram_Store_Data), .OutB(Reg_Bus_B), .OutA(Reg_Bus_A),
    .ReadB(Register_Read_To_B), .ReadA(Register_Read_To_A), .My_Address(5'b10000), .CLK(CLK));
  register register_4 (
    .Write(Register_Write), .In(Ram_Store_Data), .OutB(Reg_Bus_B), .OutA(Reg_Bus_A),
    .ReadB(Register_Read_To_B), .ReadA(Register_Read_To_A), .My_Address(5'b11000), .CLK(CLK));
  Fetch fetch_1 (
    .Instruction(Rom), .CLK(CLK), .Clear(decode_execute_1_clearprevious),
    .Instruction_2(fetch_1_instruction_2), .Condition(fetch_1_condition), .Operands(fetch_1_operands));
  register register_5 (
    .Write(Register_Write), .In(Ram_Store_Data), .OutB(Reg_Bus_B), .OutA(Reg_Bus_A),
    .ReadB(Register_Read_To_B), .ReadA(Register_Read_To_A), .My_Address(5'b00001), .CLK(CLK));
  register register_6 (
    .Write(Register_Write), .In(Ram_Store_Data), .OutB(Reg_Bus_B), .OutA(Reg_Bus_A),
    .ReadB(Register_Read_To_B), .ReadA(Register_Read_To_A), .My_Address(5'b01001), .CLK(CLK));
  register register_7 (
    .Write(Register_Write), .In(Ram_Store_Data), .OutB(Reg_Bus_B), .OutA(Reg_Bus_A),
    .ReadB(Register_Read_To_B), .ReadA(Register_Read_To_A), .My_Address(5'b10001), .CLK(CLK));
  register register_8 (
    .Write(Register_Write), .In(Ram_Store_Data), .OutB(Reg_Bus_B), .OutA(Reg_Bus_A),
    .ReadB(Register_Read_To_B), .ReadA(Register_Read_To_A), .My_Address(5'b11001), .CLK(CLK));
  Decode_Execute decode_execute_1 (
    .Status_Register(Status_Register), .Instruction(fetch_1_instruction_2), .Condition(fetch_1_condition),
    .Operands(fetch_1_operands), .CLK(CLK), .Ram_Data(Ram_Data),
    .Instruction_2(decode_execute_1_instruction_2), .Condition_2(decode_execute_1_condition_2),
    .Alu_Instructions(decode_execute_1_alu_instructions), .RegisterOut(decode_execute_1_registerout),
    .ClearPrevious(decode_execute_1_clearprevious), .ReadRegisterToA(Register_Read_To_A),
    .ReadRegisterToB(Register_Read_To_B), .PC(PC), .AluEnabled(decode_execute_1_aluenabled),
    .Load_Value(decode_execute_1_load_value),
    .RAM_Destination_Address(decode_execute_1_ram_destination_address), .RAM_Address(Ram_Address),
    .RegBusA(Reg_Bus_A), .Status_in(Status_In), .ExtraData(decode_execute_1_extradata));
  ALU alu_1 (
    .Instructions(decode_execute_1_alu_instructions), .Enable(decode_execute_1_aluenabled),
    .Reg_A(Reg_Bus_A), .Reg_B(Reg_Bus_B), .CLK(CLK), .Output_Value(decode_execute_1_load_value),
    .Status_Reg(Status_In));
  StoreResult storeresult_1 (
    .Instruction(decode_execute_1_instruction_2), .Condition(decode_execute_1_condition_2),
    .OutRegisterAddress(decode_execute_1_registerout), .Load_value(decode_execute_1_load_value),
    .Ram_Destination_Address(decode_execute_1_ram_destination_address), .CLK(CLK),
    .Register_Write(Register_Write), .DataBus(Ram_Store_Data), .RamWriteAddress(Ram_Store_Address),
    .RAM_Store(Ram_Store), .ExtraDataIn(decode_execute_1_extradata), .ExtradataOut(ExtraData));
  register register_9 (
    .Write(Register_Write), .In(Ram_Store_Data), .OutB(Reg_Bus_B), .OutA(Reg_Bus_A),
    .ReadB(Register_Read_To_B), .ReadA(Register_Read_To_A), .My_Address(5'b00010), .CLK(CLK));
  register register_10 (
    .Write(Register_Write), .In(Ram_Store_Data), .OutB(Reg_Bus_B), .OutA(Reg_Bus_A),
    .ReadB(Register_Read_To_B), .ReadA(Register_Read_To_A), .My_Address(5'b01010), .CLK(CLK));
  register register_11 (
    .Write(Register_Write), .In(Ram_Store_Data), .OutB(Reg_Bus_B), .OutA(Reg_Bus_A),
    .ReadB(Register_Read_To_B), .ReadA(Register_Read_To_A), .My_Address(5'b10010), .CLK(CLK));
  register register_12 (
    .Write(Register_Write), .In(Ram_Store_Data), .OutB(Reg_Bus_B), .OutA(Reg_Bus_A),
    .ReadB(Register_Read_To_B), .ReadA(Register_Read_To_A), .My_Address(5'b11010), .CLK(CLK));
  register register_13 (
    .Write(Register_Write), .In(Ram_Store_Data), .OutB(Reg_Bus_B), .OutA(Reg_Bus_A),
    .ReadB(Register_Read_To_B), .ReadA(Register_Read_To_A), .My_Address(5'b00011), .CLK(CLK));
  register register_14 (
    .Write(Register_Write), .In(Ram_Store_Data), .OutB(Reg_Bus_B), .OutA(Reg_Bus_A),
    .ReadB(Register_Read_To_B), .ReadA(Register_Read_To_A), .My_Address(5'b01011), .CLK(CLK));
  register register_15 (
    .Write(Register_Write), .In(Ram_Store_Data), .OutB(Reg_Bus_B), .OutA(Reg_Bus_A),
    .ReadB(Register_Read_To_B), .ReadA(Register_Read_To_A), .My_Address(5'b10011));  // open: CLK
  register register_16 (
    .Write(Register_Write), .In(Ram_Store_Data), .OutB(Reg_Bus_B), .OutA(Reg_Bus_A),
    .ReadB(Register_Read_To_B), .ReadA(Register_Read_To_A), .My_Address(5'b11011), .CLK(CLK));
  register register_17 (
    .Write(Register_Write), .In(Ram_Store_Data), .OutB(Reg_Bus_B), .OutA(Reg_Bus_A),
    .ReadB(Register_Read_To_B), .ReadA(Register_Read_To_A), .My_Address(5'b00100), .CLK(CLK));
  register register_18 (
    .Write(Register_Write), .In(Ram_Store_Data), .OutB(Reg_Bus_B), .OutA(Reg_Bus_A),
    .ReadB(Register_Read_To_B), .ReadA(Register_Read_To_A), .My_Address(5'b01100), .CLK(CLK));
  register register_19 (
    .Write(Register_Write), .In(Ram_Store_Data), .OutB(Reg_Bus_B), .OutA(Reg_Bus_A),
    .ReadB(Register_Read_To_B), .ReadA(Register_Read_To_A), .My_Address(5'b10100), .CLK(CLK));
  ImageRegister Image (.In(Ram_Store_Data), .Write(Register_Write), .My_Address(5'b11100), .OutA(Image_Index));
  register register_20 (
    .Write(Register_Write), .In(Ram_Store_Data), .OutB(Reg_Bus_B), .OutA(Reg_Bus_A),
    .ReadB(Register_Read_To_B), .ReadA(Register_Read_To_A), .My_Address(5'b00101), .CLK(CLK));
  register register_21 (
    .Write(Register_Write), .In(Ram_Store_Data), .OutB(Reg_Bus_B), .OutA(Reg_Bus_A),
    .ReadB(Register_Read_To_B), .ReadA(Register_Read_To_A), .My_Address(5'b01101), .CLK(CLK));
  register register_22 (
    .Write(Register_Write), .In(Ram_Store_Data), .OutB(Reg_Bus_B), .OutA(Reg_Bus_A),
    .ReadB(Register_Read_To_B), .ReadA(Register_Read_To_A), .My_Address(5'b10101), .CLK(CLK));
  KeyboardRegister Keyboard (
    .In(Keyboard_in), .ReadA(Register_Read_To_A), .ReadB(Register_Read_To_B), .My_Address(5'b11101),
    .Keyboard_status(Keyboard_Notempty), .OutA(Reg_Bus_A), .OutB(Reg_Bus_B), .Keyboard_Next(Keyboard_Next),
    .Status_Register(Status_In));
  register register_23 (
    .Write(Register_Write), .In(Ram_Store_Data), .OutB(Reg_Bus_B), .OutA(Reg_Bus_A),
    .ReadB(Register_Read_To_B), .ReadA(Register_Read_To_A), .My_Address(5'b00110), .CLK(CLK));
  register register_24 (
    .Write(Register_Write), .In(Ram_Store_Data), .OutB(Reg_Bus_B), .OutA(Reg_Bus_A),
    .ReadB(Register_Read_To_B), .ReadA(Register_Read_To_A), .My_Address(5'b01110), .CLK(CLK));
  register register_25 (
    .Write(Register_Write), .In(Ram_Store_Data), .OutB(Reg_Bus_B), .OutA(Reg_Bus_A),
    .ReadB(Register_Read_To_B), .ReadA(Register_Read_To_A), .My_Address(5'b10110), .CLK(CLK));
  TTYRegister TTY_Reg (
    .In(Ram_Store_Data), .Currend_Address(Register_Write), .My_Address(5'b11110), .ExtraData(ExtraData),
    .CLK(CLK), .Out(TTY_Data), .OutClk(TTY_CLK), .Status_Reg(Status_In));
  register register_26 (
    .Write(Register_Write), .In(Ram_Store_Data), .OutB(Reg_Bus_B), .OutA(Reg_Bus_A),
    .ReadB(Register_Read_To_B), .ReadA(Register_Read_To_A), .My_Address(5'b00111), .CLK(CLK));
  register register_27 (
    .Write(Register_Write), .In(Ram_Store_Data), .OutB(Reg_Bus_B), .OutA(Reg_Bus_A),
    .ReadB(Register_Read_To_B), .ReadA(Register_Read_To_A), .My_Address(5'b01111), .CLK(CLK));
  register register_28 (
    .Write(Register_Write), .In(Ram_Store_Data), .OutB(Reg_Bus_B), .OutA(Reg_Bus_A),
    .ReadB(Register_Read_To_B), .ReadA(Register_Read_To_A), .My_Address(5'b10111), .CLK(CLK));
  SR u_Status_Register (
    .SR_In(Status_In), .ReadA(Register_Read_To_A), .ReadB(Register_Read_To_B), .My_Address({5{1'b1}}),
    .OutA(Reg_Bus_A), .OutB(Reg_Bus_B), .SR_Out(Status_Register));

  // Other names for the same wires on the sheet: Data_Bus[31:0] = Ram_Store_Data
endmodule

module Fetch (
  input  [31:0] Instruction,
  input  CLK,
  input  Clear,
  output [31:0] Instruction_2,
  output [3:0] Condition,
  output [22:0] Operands
);

  wire [4:0] Instruction_t;
  wire [31:28] register_1_q;

  Register #(.width(32)) register_1 (
    .D(Instruction), .en(1'b1), .Q({register_1_q, Instruction_t, Operands}), .clk(CLK));  // open: clr
  Multiplexer #(.width(4), .disabled(0), .enable("false")) multiplexer_1 (
    .in0(register_1_q), .in1(4'b1111), .out(Condition), .sel(Clear));
  Demultiplexer #(.select(5), .disabled(0), .enable("false")) demultiplexer_1 (
    .out0(Instruction_2[0]), .out1(Instruction_2[1]), .out2(Instruction_2[2]), .out3(Instruction_2[3]),
    .out4(Instruction_2[4]), .out5(Instruction_2[5]), .out6(Instruction_2[6]), .out7(Instruction_2[7]),
    .out8(Instruction_2[8]), .out9(Instruction_2[9]), .out10(Instruction_2[10]), .out11(Instruction_2[11]),
    .out12(Instruction_2[12]), .out13(Instruction_2[13]), .out14(Instruction_2[14]),
    .out15(Instruction_2[15]), .out16(Instruction_2[16]), .out17(Instruction_2[17]),
    .out18(Instruction_2[18]), .out19(Instruction_2[19]), .out20(Instruction_2[20]),
    .out21(Instruction_2[21]), .out22(Instruction_2[22]), .out23(Instruction_2[23]),
    .out24(Instruction_2[24]), .out25(Instruction_2[25]), .out26(Instruction_2[26]),
    .out27(Instruction_2[27]), .out28(Instruction_2[28]), .out29(Instruction_2[29]),
    .out30(Instruction_2[30]), .out31(Instruction_2[31]), .in(1'b1), .sel(Instruction_t));
endmodule

// EXECUTE
module Decode_Execute (
  input  [31:0] Status_Register,
  input  [31:0] Instruction,
  input  [3:0] Condition,
  input  [22:0] Operands,
  input  CLK,
  input  [31:0] Ram_Data,
  input  [31:0] RegBusA,
  output [31:0] Instruction_2,
  output Condition_2,
  output [3:0] Alu_Instructions,
  output [4:0] RegisterOut,
  output ClearPrevious,
  output [4:0] ReadRegisterToA,
  output [4:0] ReadRegisterToB,
  output [22:0] PC,
  output AluEnabled,
  output [4:0] ExtraData,
  output [31:0] Load_Value,
  output [31:0] Status_in,
  output [17:0] RAM_Destination_Address,
  output [17:0] RAM_Address
);

  wire bitselector_1_out, BRA, checkconditions_1_out_bool, CLK_t, HLT, JMP, LDM, LDR, LDV, MOV, NOP,
       not_1_out, not_2_out, not_4_out, not_5_out, or_1_out, or_2_out, or_3_out, or_4_out, REB, register_4_q,
       register_6_q, RET, STM, STR;
  wire [17:4] Address;
  wire [22:0] adder_1_out, Current_PC, fifo_1_data_out, PC_In;
  wire [22:18] Operands_t;
  wire [29:7] multiplexer_1_out;
  wire [31:0] bit_extender_1_out, setbit_2_out_3, Status_Register_t;

  Pull_Resistor pull_resistor_1 (.node(Status_Register));
  CheckConditions checkconditions_1 (
    .Status_Register(Status_Register), .Condition(Condition), .Out_Bool(checkconditions_1_out_bool));
  and and_1 (CLK_t, CLK, not_1_out);
  not not_1 (not_1_out, HLT);
  or or_1 (or_1_out, LDV, LDR);
  or or_2 (or_2_out, STR, MOV);
  Register #(.width(23)) register_1 (.D(PC), .en(1'b1), .Q(Current_PC), .clk(CLK_t));  // open: clr
  Register #(.width(32)) register_2 (.D(Status_Register), .en(1'b1), .Q(Status_Register_t), .clk(CLK_t));  // open: clr
  Register #(.width(32)) register_3 (.D(Instruction), .en(1'b1), .Q(Instruction_2), .clk(CLK_t));  // open: clr
  Register #(.width(1)) register_4 (.D(not_2_out), .en(1'b1), .Q(register_4_q), .clk(CLK_t));  // open: clr
  not not_2 (not_2_out, checkconditions_1_out_bool);
  Register #(.width(23)) register_5 (
    .D(Operands), .en(1'b1), .Q({Operands_t, Address, Alu_Instructions}), .clk(CLK_t));  // open: clr
  or or_3 (or_3_out, AluEnabled, STR, MOV, REB);
  not not_3 (Condition_2, register_4_q);
  assign RegisterOut = or_1_out ? Operands_t : 5'bz;  // Controlled_Buffer controlled_buffer_1
  assign RegisterOut = MOV ? Address[17:13] : 5'bz;  // Controlled_Buffer controlled_buffer_2
  assign RegisterOut = AluEnabled ? Address[12:8] : 5'bz;  // Controlled_Buffer controlled_buffer_3
  assign ReadRegisterToA = or_3_out ? Operands_t : 5'bz;  // Controlled_Buffer controlled_buffer_4
  assign ReadRegisterToB = AluEnabled ? Address[17:13] : 5'bz;  // Controlled_Buffer controlled_buffer_5
  assign ExtraData = MOV ? Address[12:8] : 5'bz;  // Controlled_Buffer controlled_buffer_6
  Pull_Resistor pull_resistor_2 (.node(ExtraData));
  assign Load_Value = LDV ? bit_extender_1_out : 32'bz;  // Controlled_Buffer controlled_buffer_7
  assign bit_extender_1_out = {{14{1'b0}}, {Address, Alu_Instructions}};  // Bit_Extender bit_extender_1
  assign Load_Value = LDR ? Ram_Data : 32'bz;  // Controlled_Buffer controlled_buffer_8
  assign Load_Value = or_2_out ? RegBusA : 32'bz;  // Controlled_Buffer controlled_buffer_9
  assign RAM_Destination_Address = STR ? {Address, Alu_Instructions} : 18'bz;  // Controlled_Buffer controlled_buffer_10
  assign RAM_Address = LDR ? {Address, Alu_Instructions} : 18'bz;  // Controlled_Buffer controlled_buffer_11
  Multiplexer #(.width(32), .disabled(0), .enable("false")) multiplexer_1 (
    .in0(Instruction_2), .in1({32{1'b0}}),
    .out({HLT, NOP, multiplexer_1_out[29:13], REB, AluEnabled, RET, multiplexer_1_out[9], BRA, multiplexer_1_out[7], JMP, STM, LDM, MOV, STR, LDR, LDV}),
    .sel(register_4_q));
  or or_4 (or_4_out, JMP, BRA);
  BitSelector #(.width(32)) bitselector_1 (.in(RegBusA), .out(bitselector_1_out), .sel(Address[17:13]));
  Pull_Resistor pull_resistor_3 (.node(bitselector_1_out));
  not not_4 (not_4_out, ClearPrevious);
  or or_5 (ClearPrevious, JMP, BRA, RET);
  PC_Reg pc_reg_1 (.In(PC_In), .Write(CLK_t), .Out(PC));
  assign PC_In = or_4_out ? {Operands_t, Address, Alu_Instructions} : 23'bz;  // Controlled_Buffer controlled_buffer_12
  FIFO fifo_1 (.Data_in(Current_PC), .Push(BRA), .Pop(RET), .Data_out(fifo_1_data_out));  // open: Stack_size
  Register #(.width(1), .trigger("high")) register_6 (
    .D(bitselector_1_out), .en(1'b1), .Q(register_6_q), .clk(REB));  // open: clr
  not not_5 (not_5_out, register_6_q);
  assign PC_In = RET ? fifo_1_data_out : 23'bz;  // Controlled_Buffer controlled_buffer_13
  SetBit setbit_1 (.Bool(register_6_q), .Index(5'b00011), .out_3(Status_in));
  SetBit setbit_2 (.Bool(not_5_out), .Index(5'b01000), .out_3(setbit_2_out_3));
  Adder #(.width(23)) adder_1 (.a(23'h1), .b(Current_PC), .out(adder_1_out));  // open: cin, cout
  assign PC_In = not_4_out ? adder_1_out : 23'bz;  // Controlled_Buffer controlled_buffer_14

  // Other names for the same wires on the sheet: ALU = AluEnabled; Address[3:0] = Alu_Instructions;
  //   Operands_t[17:0] = {Address, Alu_Instructions}; PC_t[22:0] = {Operands_t, Address, Alu_Instructions};
  //   Value[17:0] = {Address, Alu_Instructions}; EXECUTE = Condition_2; PC_out[22:0] = PC;
  //   RegisterA[4:0] = Operands_t; Registers[14:0] = {Operands_t, Address[17:8]}; RegisterQ[4:0] = Address[12:8];
  //   RegisterB[4:0] = Address[17:13]

  // Notes on the sheet:
  //   Index of bit
endmodule

// Store
module StoreResult (
  input  [4:0] ExtraDataIn,
  input  [31:0] Instruction,
  input  Condition,
  input  [4:0] OutRegisterAddress,
  input  [31:0] Load_value,
  input  [17:0] Ram_Destination_Address,
  input  CLK,
  output [4:0] ExtradataOut,
  output [4:0] Register_Write,
  output [31:0] DataBus,
  output [17:0] RamWriteAddress,
  output RAM_Store
);

  wire ALU, BRA, BRAA, Condition_t, HLT, JMP, JMPA, LDM, LDR, LDV, MOV, NOP, not_1_out, or_1_out, RET, STM;
  wire [4:0] Out_Register_Address;
  wire [17:0] Ram_Destination_Address_t;
  wire [29:12] multiplexer_1_out;
  wire [31:0] Instruction_t, Load_Value_t;

  Pull_Resistor pull_resistor_1 (.node(Instruction));
  Pull_Resistor pull_resistor_2 (.node(OutRegisterAddress));
  Pull_Resistor pull_resistor_3 (.node(Load_value));
  Pull_Resistor pull_resistor_4 (.node(Ram_Destination_Address));
  or or_1 (or_1_out, LDV, MOV, LDR, ALU);
  Register #(.width(5)) register_1 (.D(ExtraDataIn), .en(1'b1), .Q(ExtradataOut), .clk(CLK));  // open: clr
  Register #(.width(32)) register_2 (.D(Instruction), .en(1'b1), .Q(Instruction_t), .clk(CLK));  // open: clr
  Register #(.width(1)) register_3 (.D(Condition), .en(1'b1), .Q(Condition_t), .clk(CLK));  // open: clr
  Register #(.width(5)) register_4 (
    .D(OutRegisterAddress), .en(1'b1), .Q(Out_Register_Address), .clk(CLK));  // open: clr
  Register #(.width(32)) register_5 (.D(Load_value), .en(1'b1), .Q(Load_Value_t), .clk(CLK));  // open: clr
  Register #(.width(18)) register_6 (
    .D(Ram_Destination_Address), .en(1'b1), .Q(Ram_Destination_Address_t), .clk(CLK));  // open: clr
  assign Register_Write = or_1_out ? Out_Register_Address : 5'bz;  // Controlled_Buffer controlled_buffer_1
  assign RamWriteAddress = RAM_Store ? Ram_Destination_Address_t : 18'bz;  // Controlled_Buffer controlled_buffer_2
  Multiplexer #(.width(32), .disabled(0), .enable("false")) multiplexer_1 (
    .in0(Instruction_t), .in1({32{1'b0}}),
    .out({HLT, NOP, multiplexer_1_out, ALU, RET, BRAA, BRA, JMPA, JMP, STM, LDM, MOV, RAM_Store, LDR, LDV}),
    .sel(not_1_out));
  not not_1 (not_1_out, Condition_t);
  assign DataBus = or_1_out ? Load_Value_t : 32'bz;  // Controlled_Buffer controlled_buffer_3
  assign DataBus = RAM_Store ? Load_Value_t : 32'bz;  // Controlled_Buffer controlled_buffer_4

  // Other names for the same wires on the sheet: STR = RAM_Store
endmodule

module ALU (
  input  [3:0] Instructions,
  input  Enable,
  input  [31:0] Reg_A,
  input  [31:0] Reg_B,
  input  CLK,
  output [31:0] Output_Value,
  output [31:0] Status_Reg
);

  wire ADD, AND, and_2_out, CMP, CMPU, comparator_1_eq, comparator_1_gt, comparator_1_lt, comparator_2_eq,
       comparator_2_gt, comparator_2_lt, DIV, Enable_t, INV, MUL, NAND, NOR, not_2_out, OR, SHL, SHR, SUB,
       XNOR, XOR;
  wire [2:0] controlled_buffer_14_out, register_5_q;
  wire [3:0] Instruction, register_1_q;
  wire [4:0] bit_extender_1_out, bit_extender_2_out;
  wire [31:0] adder_1_out, and_1_out, divider_1_out, multiplier_1_out, nand_1_out, nor_1_out, not_1_out,
       or_1_out, Reg_A_t, Reg_B_t, shifter_1_out, shifter_2_out, subtractor_1_out, xnor_1_out, xor_1_out;

  Adder #(.width(32)) adder_1 (.a(Reg_A_t), .b(Reg_B_t), .out(adder_1_out));  // open: cin, cout
  Subtractor #(.width(32)) subtractor_1 (.a(Reg_A_t), .b(Reg_B_t), .out(subtractor_1_out));  // open: bin, bout
  Multiplier #(.width(32)) multiplier_1 (.a(Reg_A_t), .b(Reg_B_t), .out(multiplier_1_out));  // open: cin, cout
  Divider #(.width(32)) divider_1 (.a(Reg_A_t), .b(Reg_B_t), .out(divider_1_out));  // open: upper, rem
  Bit_Extender #(.in_width(32), .out_width(5)) bit_extender_1 (.in(Reg_B_t), .out(bit_extender_1_out));
  Bit_Extender #(.in_width(32), .out_width(5)) bit_extender_2 (.in(Reg_B_t), .out(bit_extender_2_out));
  assign and_1_out = Reg_A_t & Reg_B_t;  // AND_Gate and_1, 32 bits wide
  assign or_1_out = Reg_A_t | Reg_B_t;  // OR_Gate or_1, 32 bits wide
  assign not_1_out = ~Reg_A_t;  // NOT_Gate not_1, 32 bits wide
  assign xor_1_out = Reg_A_t ^ Reg_B_t;  // XOR_Gate xor_1, 32 bits wide
  assign nand_1_out = ~(Reg_A_t & Reg_B_t);  // NAND_Gate nand_1, 32 bits wide
  assign nor_1_out = ~(Reg_A_t | Reg_B_t);  // NOR_Gate nor_1, 32 bits wide
  assign xnor_1_out = ~(Reg_A_t ^ Reg_B_t);  // XNOR_Gate xnor_1, 32 bits wide
  Register #(.width(4), .trigger("low")) register_1 (
    .D(Instructions), .en(1'b1), .Q(register_1_q), .clk(CLK));  // open: clr
  Register #(.width(1), .trigger("low")) register_2 (.D(Enable), .en(1'b1), .Q(Enable_t), .clk(CLK));  // open: clr
  Register #(.width(32), .trigger("low")) register_3 (.D(Reg_A), .en(1'b1), .Q(Reg_A_t), .clk(CLK));  // open: clr
  Register #(.width(32), .trigger("low")) register_4 (.D(Reg_B), .en(1'b1), .Q(Reg_B_t), .clk(CLK));  // open: clr
  assign Output_Value = ADD ? adder_1_out : 32'bz;  // Controlled_Buffer controlled_buffer_1
  assign Output_Value = SUB ? subtractor_1_out : 32'bz;  // Controlled_Buffer controlled_buffer_2
  assign Output_Value = MUL ? multiplier_1_out : 32'bz;  // Controlled_Buffer controlled_buffer_3
  assign Output_Value = DIV ? divider_1_out : 32'bz;  // Controlled_Buffer controlled_buffer_4
  Shifter #(.width(32)) shifter_1 (.in(Reg_A_t), .\dist (bit_extender_1_out), .out(shifter_1_out));
  assign Output_Value = SHL ? shifter_1_out : 32'bz;  // Controlled_Buffer controlled_buffer_5
  Shifter #(.width(32), .shift("lr")) shifter_2 (.in(Reg_A_t), .\dist (bit_extender_2_out), .out(shifter_2_out));
  assign Output_Value = SHR ? shifter_2_out : 32'bz;  // Controlled_Buffer controlled_buffer_6
  assign Output_Value = AND ? and_1_out : 32'bz;  // Controlled_Buffer controlled_buffer_7
  assign Output_Value = OR ? or_1_out : 32'bz;  // Controlled_Buffer controlled_buffer_8
  assign Output_Value = INV ? not_1_out : 32'bz;  // Controlled_Buffer controlled_buffer_9
  assign Output_Value = XOR ? xor_1_out : 32'bz;  // Controlled_Buffer controlled_buffer_10
  assign Output_Value = NAND ? nand_1_out : 32'bz;  // Controlled_Buffer controlled_buffer_11
  assign Output_Value = NOR ? nor_1_out : 32'bz;  // Controlled_Buffer controlled_buffer_12
  assign Output_Value = XNOR ? xnor_1_out : 32'bz;  // Controlled_Buffer controlled_buffer_13
  not not_2 (not_2_out, Enable_t);
  Multiplexer #(.width(4), .disabled(0), .enable("false")) multiplexer_1 (
    .in0(register_1_q), .in1(4'b1111), .out(Instruction), .sel(not_2_out));
  Comparator #(.width(32)) comparator_1 (
    .a(Reg_A_t), .b(Reg_B_t), .gt(comparator_1_gt), .eq(comparator_1_eq), .lt(comparator_1_lt));
  assign controlled_buffer_14_out[0] = CMP ? comparator_1_eq : 1'bz;  // Controlled_Buffer controlled_buffer_14
  assign controlled_buffer_14_out[2] = CMP ? comparator_1_lt : 1'bz;  // Controlled_Buffer controlled_buffer_15
  Comparator #(.width(32), .mode("unsigned")) comparator_2 (
    .a(Reg_A_t), .b(Reg_B_t), .gt(comparator_2_gt), .eq(comparator_2_eq), .lt(comparator_2_lt));
  assign controlled_buffer_14_out[0] = CMPU ? comparator_2_eq : 1'bz;  // Controlled_Buffer controlled_buffer_16
  assign controlled_buffer_14_out[2] = CMPU ? comparator_2_lt : 1'bz;  // Controlled_Buffer controlled_buffer_17
  assign controlled_buffer_14_out[1] = CMP ? comparator_1_gt : 1'bz;  // Controlled_Buffer controlled_buffer_18
  assign controlled_buffer_14_out[1] = CMPU ? comparator_2_gt : 1'bz;  // Controlled_Buffer controlled_buffer_19
  Demultiplexer #(.select(4), .disabled(0), .enable("false")) demultiplexer_1 (
    .out0(ADD), .out1(SUB), .out2(MUL), .out3(DIV), .out4(CMP), .out5(CMPU), .out6(SHL), .out7(SHR),
    .out8(AND), .out9(OR), .out10(INV), .out11(XOR), .out12(NAND), .out13(NOR), .out14(XNOR), .in(1'b1),
    .sel(Instruction));  // open: out15
  and and_2 (and_2_out, Enable_t, CLK);
  Bit_Extender #(.in_width(3), .out_width(32), .\type ("input")) bit_extender_3 (
    .in(register_5_q), .out(Status_Reg));  // open: extend
  Register #(.width(3), .trigger("low")) register_5 (
    .D(controlled_buffer_14_out), .en(1'b1), .Q(register_5_q), .clk(and_2_out));  // open: clr

  // Other names for the same wires on the sheet: OutValue[31:0] = Output_Value
endmodule

// Ram
module ram (
  input  [31:0] StoreData,
  input  [17:0] StoreAddress,
  input  [17:0] Address,
  input  Store,
  output [31:0] Data_Out
);

  RAM #(.addrWidth(18), .dataWidth(32), .bus("separate"), .addrWidth_s(18), .dataWidth_s(32)) ram_1 (
    .addr(Address), .data(Data_Out), .str(1'b0), .sel(1'b1), .clk(Store), .ld(1'b1));  // open: din, clr
  Pull_Resistor pull_resistor_1 (.node(Store));
endmodule

// Rom
module rom (
  input  [22:0] Address_In,
  output [31:0] Out
);

  ROM #(.addrWidth(23), .dataWidth(32)) rom_1 (.addr(Address_In), .data(Out));  // open: sel

  // Notes on the sheet:
  //   contents of rom_1 (hex, n*v repeats v):
  //   4000c 187c000 4002b 8002d c002f 10002a 14000a 180008 240000 280000 380030 67c8000 8300000b 1f4e000
  //   19fc000 59c2004 13000024 59c4004 13000024 59c6004 13000024 59c8004 13000024 59ca004 13000027 59cc004
  //   13000000 59dc701 5a54004 23000021 5a0a802 5a0e800 300000b 5acab02 5aceb00 300000b 19d8000 240001
  //   300000b 5b02004 1300002f 5b04004 13000031 5b06004 13000033 5b08004 13000035 5a16d00 3000037 5a16d01
  //   3000037 5a16d03 3000037 5a16d02 3000037 1b7c200 67ca000 73000038 197c000 200000 2c0000 240000 340000
  //   300000b
endmodule

// Reg
module register (
  input  [31:0] In,
  input  [4:0] Write,
  input  [4:0] ReadA,
  input  [4:0] ReadB,
  input  [4:0] My_Address,
  input  CLK,
  output [31:0] OutA,
  output [31:0] OutB
);

  wire comparator_1_eq, comparator_2_eq, pull_resistor_3_node;
  wire [31:0] controlled_buffer_1_out, register_1_q;

  Comparator #(.width(5)) comparator_1 (.a(Write), .b(My_Address), .eq(comparator_1_eq));  // open: gt, lt
  Comparator #(.width(5)) comparator_2 (.a(ReadA), .b(My_Address), .eq(comparator_2_eq));  // open: gt, lt
  Pull_Resistor pull_resistor_1 (.node(comparator_1_eq));
  Pull_Resistor pull_resistor_2 (.node(comparator_2_eq));
  Pull_Resistor pull_resistor_3 (.node(pull_resistor_3_node));
  Comparator #(.width(5)) comparator_3 (.a(ReadB), .b(My_Address), .eq(pull_resistor_3_node));  // open: gt, lt
  assign controlled_buffer_1_out = comparator_1_eq ? In : 32'bz;  // Controlled_Buffer controlled_buffer_1
  Register #(.width(32), .trigger("falling")) register_1 (
    .D(controlled_buffer_1_out), .en(1'b1), .Q(register_1_q), .clk(CLK));  // open: clr
  assign OutA = comparator_2_eq ? register_1_q : 32'bz;  // Controlled_Buffer controlled_buffer_2
  assign OutB = pull_resistor_3_node ? register_1_q : 32'bz;  // Controlled_Buffer controlled_buffer_3
endmodule

// Stack
module FIFO (
  input  [22:0] Data_in,
  input  Push,
  input  Pop,
  output [22:0] Data_out,
  output [7:0] Stack_size
);

  wire [7:0] counter_1_q, counter_2_q, multiplexer_1_out, pull_resistor_1_node;
  wire [22:0] ram_1_data;

  Counter counter_1 (.count(Push), .Q(counter_1_q), .clk(Push));  // open: load, D, carry, clr
  Counter counter_2 (.count(Pop), .Q(counter_2_q), .clk(Pop));  // open: load, D, carry, clr
  Multiplexer #(.width(8), .disabled(0), .enable("false")) multiplexer_1 (
    .in0(counter_1_q), .in1(pull_resistor_1_node), .out(multiplexer_1_out), .sel(Pop));
  Pull_Resistor pull_resistor_1 (.node(pull_resistor_1_node));
  Subtractor subtractor_1 (.a(counter_1_q), .b(counter_2_q), .out(Stack_size));  // open: bin, bout
  Subtractor subtractor_2 (.a(counter_2_q), .b(8'h1), .out(pull_resistor_1_node));  // open: bin, bout
  RAM #(.dataWidth(23), .bus("separate")) ram_1 (
    .addr(multiplexer_1_out), .din(Data_in), .data(ram_1_data), .clk(Push), .ld(1'b1));  // open: str, sel, clr
  Register #(.width(23), .trigger("high")) register_1 (
    .D(ram_1_data), .en(1'b1), .Q(Data_out), .clk(Pop));  // open: clr
endmodule

// PC
module PC_Reg (
  input  [22:0] In,
  input  Write,
  output [22:0] Out
);

  Register #(.width(23), .trigger("falling")) register_1 (.D(In), .en(1'b1), .Q(Out), .clk(Write));  // open: clr
endmodule

module SR (
  input  [31:0] SR_In,
  input  [4:0] ReadA,
  input  [4:0] ReadB,
  input  [4:0] My_Address,
  output [31:0] OutA,
  output [31:0] OutB,
  output [31:0] SR_Out
);

  wire comparator_1_eq, comparator_2_eq;

  Comparator #(.width(5)) comparator_1 (.a(ReadA), .b(My_Address), .eq(comparator_1_eq));  // open: gt, lt
  Comparator #(.width(5)) comparator_2 (.a(ReadB), .b(My_Address), .eq(comparator_2_eq));  // open: gt, lt
  Pull_Resistor pull_resistor_1 (.node(comparator_1_eq));
  assign OutA = comparator_1_eq ? SR_In : 32'bz;  // Controlled_Buffer controlled_buffer_1
  Pull_Resistor pull_resistor_2 (.node(comparator_2_eq));
  assign OutB = comparator_2_eq ? SR_In : 32'bz;  // Controlled_Buffer controlled_buffer_2

  assign SR_Out = SR_In;
endmodule

// TTY
module TTYRegister (
  input  [31:0] In,
  input  [4:0] Currend_Address,
  input  [4:0] My_Address,
  input  [4:0] ExtraData,
  input  CLK,
  output [6:0] Out,
  output OutClk,
  output [31:0] Status_Reg
);

  wire and_1_out, and_2_out, and_3_out, and_4_p3, comparator_2_eq, comparator_3_eq, comparator_4_eq,
       comparator_5_eq, comparator_6_eq, not_1_out, not_2_out, Number, SendSignal, WriteInt;
  wire [3:0] counter_1_q;
  wire [6:0] bintobcd_1__1, bintobcd_1__1_000, bintobcd_1__1_000_000, bintobcd_1__1_000_000_000,
       bintobcd_1__10, bintobcd_1__10_000, bintobcd_1__10_000_000, bintobcd_1__100, bintobcd_1__100_000,
       bintobcd_1__100_000_000, bit_extender_1_out, multiplexer_1_out;
  wire [31:0] buffer_1_out, buffer_2_out, buffer_3_out, buffer_4_out, buffer_5_out, buffer_6_out,
       buffer_7_out, buffer_8_out, Data;

  assign buffer_1_out = buffer_2_out;  // Buffer buffer_1, 32 bits wide
  assign buffer_2_out = buffer_3_out;  // Buffer buffer_2, 32 bits wide
  assign buffer_3_out = buffer_4_out;  // Buffer buffer_3, 32 bits wide
  assign buffer_4_out = In;  // Buffer buffer_4, 32 bits wide
  Comparator #(.width(5)) comparator_1 (.a(Currend_Address), .b(My_Address), .eq(SendSignal));  // open: gt, lt
  assign buffer_5_out = buffer_6_out;  // Buffer buffer_5, 32 bits wide
  assign buffer_6_out = buffer_1_out;  // Buffer buffer_6, 32 bits wide
  assign buffer_7_out = buffer_5_out;  // Buffer buffer_7, 32 bits wide
  assign buffer_8_out = buffer_7_out;  // Buffer buffer_8, 32 bits wide
  Pull_Resistor pull_resistor_1 (.node(SendSignal));
  Register #(.width(32), .trigger("high")) register_1 (
    .D(buffer_8_out), .en(1'b1), .Q(Data), .clk(SendSignal));  // open: clr
  Comparator #(.width(5)) comparator_2 (.a(ExtraData), .b({5{1'b0}}), .eq(comparator_2_eq));  // open: gt, lt
  Comparator #(.width(5)) comparator_3 (.a(ExtraData), .b(5'b00001), .eq(comparator_3_eq));  // open: gt, lt
  Comparator #(.width(5)) comparator_4 (.a(ExtraData), .b(5'b00010), .eq(comparator_4_eq));  // open: gt, lt
  Comparator #(.width(5)) comparator_5 (.a(ExtraData), .b(5'b00011), .eq(comparator_5_eq));  // open: gt, lt
  assign Out = and_1_out ? bit_extender_1_out : 7'bz;  // Controlled_Buffer controlled_buffer_1
  Bit_Extender #(.in_width(32), .out_width(7)) bit_extender_1 (.in(Data), .out(bit_extender_1_out));
  and and_1 (and_1_out, SendSignal, comparator_2_eq);
  or or_1 (Number, comparator_3_eq, comparator_4_eq, comparator_5_eq);
  and and_2 (and_2_out, and_1_out, not_1_out);
  not not_1 (not_1_out, CLK);
  assign OutClk = and_2_out ? 1'b1 : 1'bz;  // Controlled_Buffer controlled_buffer_2
  BinToBCD bintobcd_1 (
    .In(Data), ._1(bintobcd_1__1), ._10(bintobcd_1__10), ._100(bintobcd_1__100), ._1_000(bintobcd_1__1_000),
    ._10_000(bintobcd_1__10_000), ._100_000(bintobcd_1__100_000), ._1_000_000(bintobcd_1__1_000_000),
    ._10_000_000(bintobcd_1__10_000_000), ._100_000_000(bintobcd_1__100_000_000),
    ._1_000_000_000(bintobcd_1__1_000_000_000));
  Counter #(.width(4), .max('hb)) counter_1 (
    .count(1'b1), .Q(counter_1_q), .clk(CLK), .clr(not_2_out));  // open: load, D, carry
  not not_2 (not_2_out, WriteInt);
  Multiplexer #(.select(4), .width(7), .disabled(0), .enable("false")) multiplexer_1 (
    .in0(bintobcd_1__1_000_000_000), .in1(bintobcd_1__100_000_000), .in2(bintobcd_1__10_000_000),
    .in3(bintobcd_1__1_000_000), .in4(bintobcd_1__100_000), .in5(bintobcd_1__10_000),
    .in6(bintobcd_1__1_000), .in7(bintobcd_1__100), .in8(bintobcd_1__10), .in9(bintobcd_1__1),
    .out(multiplexer_1_out), .sel(counter_1_q));  // open: in10, in11, in12, in13, in14, in15
  assign Out = WriteInt ? multiplexer_1_out : 7'bz;  // Controlled_Buffer controlled_buffer_3
  // NOT_Gate not_3 has open pins: in=CLK, out=open
  Comparator #(.width(4), .mode("unsigned")) comparator_6 (
    .a(counter_1_q), .b(4'b1010), .eq(comparator_6_eq));  // open: gt, lt
  assign OutClk = and_3_out ? 1'b1 : 1'bz;  // Controlled_Buffer controlled_buffer_4
  and and_3 (and_3_out, WriteInt, WriteInt, CLK, CLK);
  // AND_Gate and_4: pin names not known; wires that end beside it: Number, SendSignal, and_4_p3
  S_R_Flip_Flop #(.trigger("high")) s_r_ff_1 (
    .S(and_4_p3), .clk(1'b1), .R(comparator_6_eq), .Q(WriteInt));  // open: Qn, preset, reset, en
  SetBit setbit_1 (.Bool(WriteInt), .Index(5'b00101), .out_3(Status_Reg));
  Pull_Resistor pull_resistor_2 (.node(OutClk));

  // Notes on the sheet:
  //   Ascii
  //   Signed
  //   Unsigned
  //   Float
endmodule

// KEY
module KeyboardRegister (
  input  [6:0] In,
  input  [4:0] ReadA,
  input  [4:0] ReadB,
  input  [4:0] My_Address,
  input  Keyboard_status,
  output [31:0] OutA,
  output [31:0] OutB,
  output Keyboard_Next,
  output [31:0] Status_Register
);

  wire comparator_1_eq, comparator_2_eq;
  wire [31:0] bit_extender_1_out, register_1_q;

  assign bit_extender_1_out = {{25{1'b0}}, In};  // Bit_Extender bit_extender_1
  Comparator #(.width(5)) comparator_1 (.a(ReadA), .b(My_Address), .eq(comparator_1_eq));  // open: gt, lt
  SetBit setbit_1 (.Bool(Keyboard_status), .Index(5'b00100), .out_3(Status_Register));
  Register #(.width(32)) register_1 (
    .D(bit_extender_1_out), .en(1'b1), .Q(register_1_q), .clk(Keyboard_Next));  // open: clr
  Comparator #(.width(5)) comparator_2 (.a(ReadB), .b(My_Address), .eq(comparator_2_eq));  // open: gt, lt
  assign OutA = comparator_1_eq ? register_1_q : 32'bz;  // Controlled_Buffer controlled_buffer_1
  Pull_Resistor pull_resistor_1 (.node(comparator_1_eq));
  or or_1 (Keyboard_Next, comparator_2_eq, comparator_1_eq);
  assign OutB = comparator_2_eq ? register_1_q : 32'bz;  // Controlled_Buffer controlled_buffer_2
  Pull_Resistor pull_resistor_2 (.node(comparator_2_eq));
endmodule

// IMG
module ImageRegister (
  input  [31:0] In,
  input  [4:0] Write,
  input  [4:0] My_Address,
  output [7:0] OutA
);

  wire comparator_1_eq;
  wire [31:0] register_1_q;

  Comparator #(.width(5)) comparator_1 (.a(Write), .b(My_Address), .eq(comparator_1_eq));  // open: gt, lt
  Register #(.width(32), .trigger("high")) register_1 (
    .D(In), .en(1'b1), .Q(register_1_q), .clk(comparator_1_eq));  // open: clr
  Pull_Resistor pull_resistor_1 (.node(comparator_1_eq));
  Bit_Extender #(.in_width(32), .out_width(8)) bit_extender_1 (.in(register_1_q), .out(OutA));
endmodule

module CheckConditions (
  input  [31:0] Status_Register,
  input  [3:0] Condition,
  output Out_Bool
);

  wire ALW, EQ, FAL, GEQ, GT, LEQ, LT, NEQ, NOP, not_1_out, not_2_out, or_1_out, or_2_out, TRU;

  Demultiplexer #(.select(4), .disabled(0), .enable("false")) demultiplexer_1 (
    .out0(ALW), .out1(EQ), .out2(NEQ), .out3(GT), .out4(GEQ), .out5(LT), .out6(LEQ), .out7(TRU), .out8(FAL),
    .out15(NOP), .in(1'b1), .sel(Condition));  // open: out9, out10, out11, out12, out13, out14
  assign Out_Bool = EQ ? Status_Register[0] : 1'bz;  // Controlled_Buffer controlled_buffer_1
  assign Out_Bool = NEQ ? not_1_out : 1'bz;  // Controlled_Buffer controlled_buffer_2
  not not_1 (not_1_out, Status_Register[0]);
  assign Out_Bool = GT ? Status_Register[1] : 1'bz;  // Controlled_Buffer controlled_buffer_3
  assign Out_Bool = GEQ ? or_1_out : 1'bz;  // Controlled_Buffer controlled_buffer_4
  or or_1 (or_1_out, Status_Register[0], Status_Register[1]);
  assign Out_Bool = LT ? Status_Register[2] : 1'bz;  // Controlled_Buffer controlled_buffer_5
  or or_2 (or_2_out, Status_Register[0], Status_Register[2]);
  assign Out_Bool = LEQ ? or_2_out : 1'bz;  // Controlled_Buffer controlled_buffer_6
  assign Out_Bool = TRU ? Status_Register[3] : 1'bz;  // Controlled_Buffer controlled_buffer_7
  assign Out_Bool = FAL ? not_2_out : 1'bz;  // Controlled_Buffer controlled_buffer_8
  not not_2 (not_2_out, Status_Register[3]);
  assign Out_Bool = ALW ? 1'b1 : 1'bz;  // Controlled_Buffer controlled_buffer_9
  assign Out_Bool = NOP ? 1'b0 : 1'bz;  // Controlled_Buffer controlled_buffer_10
  Pull_Resistor pull_resistor_1 (.node(Out_Bool));

  // Other names for the same wires on the sheet: Out = Out_Bool
endmodule

module SetBit (
  input  Bool,
  input  [4:0] Index,
  output [31:0] out_3
);

  Demultiplexer #(.select(5), .tristate("true"), .enable("false")) demultiplexer_1 (
    .out0(out_3[0]), .out1(out_3[1]), .out2(out_3[2]), .out3(out_3[3]), .out4(out_3[4]), .out5(out_3[5]),
    .out6(out_3[6]), .out7(out_3[7]), .out8(out_3[8]), .out9(out_3[9]), .out10(out_3[10]), .out11(out_3[11]),
    .out12(out_3[12]), .out13(out_3[13]), .out14(out_3[14]), .out15(out_3[15]), .out16(out_3[16]),
    .out17(out_3[17]), .out18(out_3[18]), .out19(out_3[19]), .out20(out_3[20]), .out21(out_3[21]),
    .out22(out_3[22]), .out23(out_3[23]), .out24(out_3[24]), .out25(out_3[25]), .out26(out_3[26]),
    .out27(out_3[27]), .out28(out_3[28]), .out29(out_3[29]), .out30(out_3[30]), .out31(out_3[31]), .in(Bool),
    .sel(Index));
endmodule

module equals (
  input  [7:0] B,
  input  [7:0] A,
  output Out
);

  Comparator comparator_1 (.a(B), .b(A), .eq(Out));  // open: gt, lt
endmodule

// <X<
module Isinside (
  input  [7:0] Value,
  input  [7:0] Smaller_limit,
  input  [7:0] Larger_limit,
  output [7:0] Value_Out,
  output Out
);

  wire comparator_1_eq, comparator_1_gt, comparator_2_eq, comparator_2_lt, or_1_out, or_2_out;

  Comparator #(.mode("unsigned")) comparator_1 (
    .a(Value), .b(Smaller_limit), .gt(comparator_1_gt), .eq(comparator_1_eq));  // open: lt
  Comparator #(.mode("unsigned")) comparator_2 (
    .a(Value), .b(Larger_limit), .eq(comparator_2_eq), .lt(comparator_2_lt));  // open: gt
  or or_1 (or_1_out, comparator_1_gt, comparator_1_eq);
  or or_2 (or_2_out, comparator_2_eq, comparator_2_lt);
  and and_1 (Out, or_1_out, or_2_out);

  assign Value_Out = Value;
endmodule

module Split (
  input  [31:0] In,
  output [3:0] Out_0,
  output [3:0] Out_1,
  output [3:0] Out_2,
  output [3:0] Out_3,
  output [3:0] Out_4,
  output [3:0] Out_5,
  output [3:0] Out_6,
  output [3:0] Out_7
);


  assign Out_0 = In[3:0];
  assign Out_1 = In[7:4];
  assign Out_2 = In[11:8];
  assign Out_3 = In[15:12];
  assign Out_4 = In[19:16];
  assign Out_5 = In[23:20];
  assign Out_6 = In[27:24];
  assign Out_7 = In[31:28];
endmodule

module BinToBCD (
  input  [31:0] In,
  output [6:0] _1,
  output [6:0] _10,
  output [6:0] _100,
  output [6:0] _1_000,
  output [6:0] _10_000,
  output [6:0] _100_000,
  output [6:0] _1_000_000,
  output [6:0] _10_000_000,
  output [6:0] _100_000_000,
  output [6:0] _1_000_000_000
);

  wire add3_1_out_0, add3_1_out_1, add3_1_out_2, add3_1_out_3, add3_2_out_0, add3_2_out_1, add3_2_out_2,
       add3_2_out_3, add3_3_out_0, add3_3_out_1, add3_3_out_2, add3_3_out_3, add3_4_out_0, add3_4_out_1,
       add3_4_out_2, add3_4_out_3, add3_5_out_0, add3_5_out_1, add3_5_out_2, add3_5_out_3, add3_6_out_0,
       add3_6_out_1, add3_6_out_2, add3_6_out_3, add3_7_out_0, add3_7_out_1, add3_7_out_2, add3_7_out_3,
       add3_8_out_0, add3_8_out_1, add3_8_out_2, add3_8_out_3, add3_9_out_0, add3_9_out_1, add3_9_out_2,
       add3_9_out_3, add3_10_out_0, add3_10_out_1, add3_10_out_2, add3_10_out_3, add3_11_out_0,
       add3_11_out_1, add3_11_out_2, add3_11_out_3, add3_12_out_0, add3_12_out_1, add3_12_out_2,
       add3_12_out_3, add3_13_out_0, add3_13_out_1, add3_13_out_2, add3_13_out_3, add3_14_out_0,
       add3_14_out_1, add3_14_out_2, add3_14_out_3, add3_15_out_0, add3_15_out_1, add3_15_out_2,
       add3_15_out_3, add3_16_out_0, add3_16_out_1, add3_16_out_2, add3_16_out_3, add3_17_out_0,
       add3_17_out_1, add3_17_out_2, add3_17_out_3, add3_18_out_0, add3_18_out_1, add3_18_out_2,
       add3_18_out_3, add3_19_out_0, add3_19_out_1, add3_19_out_2, add3_19_out_3, add3_20_out_0,
       add3_20_out_1, add3_20_out_2, add3_20_out_3, add3_21_out_0, add3_21_out_1, add3_21_out_2,
       add3_21_out_3, add3_22_out_0, add3_22_out_1, add3_22_out_2, add3_22_out_3, add3_23_out_0,
       add3_23_out_1, add3_23_out_2, add3_23_out_3, add3_24_out_0, add3_24_out_1, add3_24_out_2,
       add3_24_out_3, add3_25_out_0, add3_25_out_1, add3_25_out_2, add3_25_out_3, add3_26_out_0,
       add3_26_out_1, add3_26_out_2, add3_26_out_3, add3_27_out_0, add3_27_out_1, add3_27_out_2,
       add3_27_out_3, add3_28_out_0, add3_28_out_1, add3_28_out_2, add3_28_out_3, add3_29_out_0,
       add3_29_out_1, add3_29_out_2, add3_29_out_3, add3_30_out_0, add3_30_out_1, add3_30_out_2,
       add3_30_out_3, add3_31_out_0, add3_31_out_1, add3_31_out_2, add3_31_out_3, add3_32_out_0,
       add3_32_out_1, add3_32_out_2, add3_32_out_3, add3_33_out_0, add3_33_out_1, add3_33_out_2,
       add3_33_out_3, add3_34_out_0, add3_34_out_1, add3_34_out_2, add3_34_out_3, add3_35_out_0,
       add3_35_out_1, add3_35_out_2, add3_35_out_3, add3_36_out_0, add3_36_out_1, add3_36_out_2,
       add3_36_out_3, add3_37_out_0, add3_37_out_1, add3_37_out_2, add3_37_out_3, add3_38_out_0,
       add3_38_out_1, add3_38_out_2, add3_38_out_3, add3_39_out_0, add3_39_out_1, add3_39_out_2,
       add3_39_out_3, add3_40_out_0, add3_40_out_1, add3_40_out_2, add3_40_out_3, add3_41_out_0,
       add3_41_out_1, add3_41_out_2, add3_41_out_3, add3_42_out_0, add3_42_out_1, add3_42_out_2,
       add3_42_out_3, add3_43_out_0, add3_43_out_1, add3_43_out_2, add3_43_out_3, add3_44_out_0,
       add3_44_out_1, add3_44_out_2, add3_44_out_3, add3_45_out_0, add3_45_out_1, add3_45_out_2,
       add3_45_out_3, add3_46_out_0, add3_46_out_1, add3_46_out_2, add3_46_out_3, add3_47_out_0,
       add3_47_out_1, add3_47_out_2, add3_47_out_3, add3_48_out_0, add3_48_out_1, add3_48_out_2,
       add3_48_out_3, add3_49_out_0, add3_49_out_1, add3_49_out_2, add3_49_out_3, add3_50_out_0,
       add3_50_out_1, add3_50_out_2, add3_50_out_3, add3_51_out_0, add3_51_out_1, add3_51_out_2,
       add3_51_out_3, add3_52_out_0, add3_52_out_1, add3_52_out_2, add3_52_out_3, add3_53_out_0,
       add3_53_out_1, add3_53_out_2, add3_53_out_3, add3_54_out_0, add3_54_out_1, add3_54_out_2,
       add3_54_out_3, add3_55_out_0, add3_55_out_1, add3_55_out_2, add3_55_out_3, add3_56_out_0,
       add3_56_out_1, add3_56_out_2, add3_56_out_3, add3_57_out_0, add3_57_out_1, add3_57_out_2,
       add3_57_out_3, add3_58_out_0, add3_58_out_1, add3_58_out_2, add3_58_out_3, add3_59_out_0,
       add3_59_out_1, add3_59_out_2, add3_59_out_3, add3_60_out_0, add3_60_out_1, add3_60_out_2,
       add3_60_out_3, add3_61_out_0, add3_61_out_1, add3_61_out_2, add3_61_out_3, add3_62_out_0,
       add3_62_out_1, add3_62_out_2, add3_62_out_3, add3_63_out_0, add3_63_out_1, add3_63_out_2,
       add3_63_out_3, add3_64_out_0, add3_64_out_1, add3_64_out_2, add3_64_out_3, add3_65_out_0,
       add3_65_out_1, add3_65_out_2, add3_65_out_3, add3_66_out_0, add3_66_out_1, add3_66_out_2,
       add3_66_out_3, add3_67_out_0, add3_67_out_1, add3_67_out_2, add3_67_out_3, add3_68_out_0,
       add3_68_out_1, add3_68_out_2, add3_68_out_3, add3_69_out_0, add3_69_out_1, add3_69_out_2,
       add3_69_out_3, add3_70_out_0, add3_70_out_1, add3_70_out_2, add3_70_out_3, add3_71_out_0,
       add3_71_out_1, add3_71_out_2, add3_71_out_3, add3_72_out_0, add3_72_out_1, add3_72_out_2,
       add3_72_out_3, add3_73_out_0, add3_73_out_1, add3_73_out_2, add3_73_out_3, add3_74_out_0,
       add3_74_out_1, add3_74_out_2, add3_74_out_3, add3_75_out_0, add3_75_out_1, add3_75_out_2,
       add3_75_out_3, add3_76_out_0, add3_76_out_1, add3_76_out_2, add3_76_out_3, add3_77_out_0,
       add3_77_out_1, add3_77_out_2, add3_77_out_3, add3_78_out_0, add3_78_out_1, add3_78_out_2,
       add3_78_out_3, add3_79_out_0, add3_79_out_1, add3_79_out_2, add3_79_out_3, add3_80_out_0,
       add3_80_out_1, add3_80_out_2, add3_80_out_3, add3_81_out_0, add3_81_out_1, add3_81_out_2,
       add3_81_out_3, add3_82_out_0, add3_82_out_1, add3_82_out_2, add3_82_out_3, add3_83_out_0,
       add3_83_out_1, add3_83_out_2, add3_83_out_3, add3_84_out_0, add3_84_out_1, add3_84_out_2,
       add3_84_out_3, add3_85_out_0, add3_85_out_1, add3_85_out_2, add3_85_out_3, add3_86_out_0,
       add3_86_out_1, add3_86_out_2, add3_86_out_3, add3_87_out_0, add3_87_out_1, add3_87_out_2,
       add3_87_out_3, add3_88_out_0, add3_88_out_1, add3_88_out_2, add3_88_out_3, add3_89_out_0,
       add3_89_out_1, add3_89_out_2, add3_89_out_3, add3_90_out_0, add3_90_out_1, add3_90_out_2,
       add3_90_out_3, add3_91_out_0, add3_91_out_1, add3_91_out_2, add3_91_out_3, add3_92_out_0,
       add3_92_out_1, add3_92_out_2, add3_92_out_3, add3_93_out_0, add3_93_out_1, add3_93_out_2,
       add3_93_out_3, add3_94_out_0, add3_94_out_1, add3_94_out_2, add3_94_out_3, add3_95_out_0,
       add3_95_out_1, add3_95_out_2, add3_95_out_3, add3_96_out_0, add3_96_out_1, add3_96_out_2,
       add3_96_out_3, add3_97_out_0, add3_97_out_1, add3_97_out_2, add3_97_out_3, add3_98_out_0,
       add3_98_out_1, add3_98_out_2, add3_98_out_3, add3_99_out_0, add3_99_out_1, add3_99_out_2,
       add3_99_out_3, add3_100_out_0, add3_100_out_1, add3_100_out_2, add3_100_out_3, add3_101_out_0,
       add3_101_out_1, add3_101_out_2, add3_101_out_3, add3_102_out_0, add3_102_out_1, add3_102_out_2,
       add3_102_out_3, add3_103_out_0, add3_103_out_1, add3_103_out_2, add3_103_out_3, add3_104_out_0,
       add3_104_out_1, add3_104_out_2, add3_104_out_3, add3_105_out_0, add3_105_out_1, add3_105_out_2,
       add3_105_out_3, add3_106_out_0, add3_106_out_1, add3_106_out_2, add3_106_out_3, add3_107_out_0,
       add3_107_out_1, add3_107_out_2, add3_107_out_3, add3_108_out_0, add3_108_out_1, add3_108_out_2,
       add3_108_out_3, add3_109_out_0, add3_109_out_1, add3_109_out_2, add3_109_out_3, add3_110_out_0,
       add3_110_out_1, add3_110_out_2, add3_110_out_3, add3_111_out_0, add3_111_out_1, add3_111_out_2,
       add3_111_out_3, add3_112_out_0, add3_112_out_1, add3_112_out_2, add3_112_out_3, add3_113_out_0,
       add3_113_out_1, add3_113_out_2, add3_113_out_3, add3_114_out_0, add3_114_out_1, add3_114_out_2,
       add3_114_out_3, add3_115_out_0, add3_115_out_1, add3_115_out_2, add3_115_out_3, add3_116_out_0,
       add3_116_out_1, add3_116_out_2, add3_116_out_3, add3_117_out_0, add3_117_out_1, add3_117_out_2,
       add3_117_out_3, add3_118_out_0, add3_118_out_1, add3_118_out_2, add3_118_out_3, add3_119_out_0,
       add3_119_out_1, add3_119_out_2, add3_119_out_3, add3_120_out_0, add3_120_out_1, add3_120_out_2,
       add3_120_out_3, add3_121_out_0, add3_121_out_1, add3_121_out_2, add3_121_out_3, add3_122_out_0,
       add3_122_out_1, add3_122_out_2, add3_122_out_3, add3_123_out_0, add3_123_out_1, add3_123_out_2,
       add3_123_out_3, add3_124_out_0, add3_124_out_1, add3_124_out_2, add3_124_out_3, add3_125_out_0,
       add3_125_out_1, add3_125_out_2, add3_125_out_3, add3_126_out_0, add3_126_out_1, add3_126_out_2,
       add3_126_out_3, add3_127_out_0, add3_127_out_1, add3_127_out_2, add3_127_out_3, add3_128_out_0,
       add3_128_out_1, add3_128_out_2, add3_128_out_3, add3_129_out_0, add3_129_out_1, add3_129_out_2,
       add3_129_out_3, add3_130_out_0, add3_130_out_1, add3_130_out_2, add3_130_out_3, add3_131_out_0,
       add3_131_out_1, add3_131_out_2, add3_131_out_3, add3_132_out_0, add3_132_out_1, add3_132_out_2,
       add3_132_out_3, add3_133_out_0, add3_133_out_1, add3_133_out_2, add3_133_out_3, add3_134_out_0,
       add3_134_out_1, add3_134_out_2, add3_134_out_3, add3_135_out_0, add3_135_out_1, add3_135_out_2,
       add3_135_out_3, add3_136_out_0, add3_136_out_1, add3_136_out_2, add3_136_out_3, add3_137_out_0,
       add3_137_out_1, add3_137_out_2, add3_137_out_3, add3_138_out_0, add3_138_out_1, add3_138_out_2,
       add3_138_out_3, add3_139_out_0, add3_139_out_1, add3_139_out_2, add3_139_out_3, add3_140_out_0,
       add3_140_out_1, add3_140_out_2, add3_140_out_3, add3_141_out_0, add3_141_out_1, add3_141_out_2,
       add3_141_out_3, add3_142_out_0, add3_142_out_1, add3_142_out_2, add3_142_out_3, add3_143_out_0,
       add3_143_out_1, add3_143_out_2, add3_143_out_3, add3_144_out_0, add3_144_out_1, add3_144_out_2,
       add3_144_out_3, add3_145_out_0, add3_145_out_1, add3_145_out_2;
  wire [3:0] add3_146_out_3, add3_147_out_3, add3_148_out_3, add3_149_out_3, add3_150_out_3, add3_151_out_3,
       add3_152_out_3, add3_153_out_3, add3_154_out_3;
  wire [3:1] add3_146_out_0;

  Add3 add3_1 (
    .In0(In[29]), .In1(In[30]), .In2(In[31]), .In3(1'b0), .Out_0(add3_1_out_0), .Out_1(add3_1_out_1),
    .Out_2(add3_1_out_2), .Out_3(add3_1_out_3));
  Add3 add3_2 (
    .In0(In[26]), .In1(add3_3_out_0), .In2(add3_3_out_1), .In3(add3_3_out_2), .Out_0(add3_2_out_0),
    .Out_1(add3_2_out_1), .Out_2(add3_2_out_2), .Out_3(add3_2_out_3));
  Add3 add3_3 (
    .In0(In[27]), .In1(add3_4_out_0), .In2(add3_4_out_1), .In3(add3_4_out_2), .Out_0(add3_3_out_0),
    .Out_1(add3_3_out_1), .Out_2(add3_3_out_2), .Out_3(add3_3_out_3));
  Add3 add3_4 (
    .In0(In[28]), .In1(add3_1_out_0), .In2(add3_1_out_1), .In3(add3_1_out_2), .Out_0(add3_4_out_0),
    .Out_1(add3_4_out_1), .Out_2(add3_4_out_2), .Out_3(add3_4_out_3));
  Add3 add3_5 (
    .In0(add3_3_out_3), .In1(add3_4_out_3), .In2(add3_1_out_3), .In3(1'b0), .Out_0(add3_5_out_0),
    .Out_1(add3_5_out_1), .Out_2(add3_5_out_2), .Out_3(add3_5_out_3));
  Add3 add3_6 (
    .In0(In[24]), .In1(add3_7_out_0), .In2(add3_7_out_1), .In3(add3_7_out_2), .Out_0(add3_6_out_0),
    .Out_1(add3_6_out_1), .Out_2(add3_6_out_2), .Out_3(add3_6_out_3));
  Add3 add3_7 (
    .In0(In[25]), .In1(add3_2_out_0), .In2(add3_2_out_1), .In3(add3_2_out_2), .Out_0(add3_7_out_0),
    .Out_1(add3_7_out_1), .Out_2(add3_7_out_2), .Out_3(add3_7_out_3));
  Add3 add3_8 (
    .In0(add3_7_out_3), .In1(add3_9_out_0), .In2(add3_9_out_1), .In3(add3_9_out_2), .Out_0(add3_8_out_0),
    .Out_1(add3_8_out_1), .Out_2(add3_8_out_2), .Out_3(add3_8_out_3));
  Add3 add3_9 (
    .In0(add3_2_out_3), .In1(add3_5_out_0), .In2(add3_5_out_1), .In3(add3_5_out_2), .Out_0(add3_9_out_0),
    .Out_1(add3_9_out_1), .Out_2(add3_9_out_2), .Out_3(add3_9_out_3));
  Add3 add3_10 (
    .In0(In[21]), .In1(add3_11_out_0), .In2(add3_11_out_1), .In3(add3_11_out_2), .Out_0(add3_10_out_0),
    .Out_1(add3_10_out_1), .Out_2(add3_10_out_2), .Out_3(add3_10_out_3));
  Add3 add3_11 (
    .In0(In[22]), .In1(add3_12_out_0), .In2(add3_12_out_1), .In3(add3_12_out_2), .Out_0(add3_11_out_0),
    .Out_1(add3_11_out_1), .Out_2(add3_11_out_2), .Out_3(add3_11_out_3));
  Add3 add3_12 (
    .In0(In[23]), .In1(add3_6_out_0), .In2(add3_6_out_1), .In3(add3_6_out_2), .Out_0(add3_12_out_0),
    .Out_1(add3_12_out_1), .Out_2(add3_12_out_2), .Out_3(add3_12_out_3));
  Add3 add3_13 (
    .In0(add3_11_out_3), .In1(add3_14_out_0), .In2(add3_14_out_1), .In3(add3_14_out_2),
    .Out_0(add3_13_out_0), .Out_1(add3_13_out_1), .Out_2(add3_13_out_2), .Out_3(add3_13_out_3));
  Add3 add3_14 (
    .In0(add3_12_out_3), .In1(add3_15_out_0), .In2(add3_15_out_1), .In3(add3_15_out_2),
    .Out_0(add3_14_out_0), .Out_1(add3_14_out_1), .Out_2(add3_14_out_2), .Out_3(add3_14_out_3));
  Add3 add3_15 (
    .In0(add3_6_out_3), .In1(add3_8_out_0), .In2(add3_8_out_1), .In3(add3_8_out_2), .Out_0(add3_15_out_0),
    .Out_1(add3_15_out_1), .Out_2(add3_15_out_2), .Out_3(add3_15_out_3));
  Add3 add3_16 (
    .In0(add3_14_out_3), .In1(add3_17_out_0), .In2(add3_17_out_1), .In3(add3_17_out_2),
    .Out_0(add3_16_out_0), .Out_1(add3_16_out_1), .Out_2(add3_16_out_2), .Out_3(add3_16_out_3));
  Add3 add3_17 (
    .In0(add3_15_out_3), .In1(add3_18_out_0), .In2(add3_18_out_1), .In3(add3_18_out_2),
    .Out_0(add3_17_out_0), .Out_1(add3_17_out_1), .Out_2(add3_17_out_2), .Out_3(add3_17_out_3));
  Add3 add3_18 (
    .In0(add3_8_out_3), .In1(add3_9_out_3), .In2(add3_5_out_3), .In3(1'b0), .Out_0(add3_18_out_0),
    .Out_1(add3_18_out_1), .Out_2(add3_18_out_2), .Out_3(add3_18_out_3));
  Add3 add3_19 (
    .In0(In[18]), .In1(add3_20_out_0), .In2(add3_20_out_1), .In3(add3_20_out_2), .Out_0(add3_19_out_0),
    .Out_1(add3_19_out_1), .Out_2(add3_19_out_2), .Out_3(add3_19_out_3));
  Add3 add3_20 (
    .In0(In[19]), .In1(add3_21_out_0), .In2(add3_21_out_1), .In3(add3_21_out_2), .Out_0(add3_20_out_0),
    .Out_1(add3_20_out_1), .Out_2(add3_20_out_2), .Out_3(add3_20_out_3));
  Add3 add3_21 (
    .In0(In[20]), .In1(add3_10_out_0), .In2(add3_10_out_1), .In3(add3_10_out_2), .Out_0(add3_21_out_0),
    .Out_1(add3_21_out_1), .Out_2(add3_21_out_2), .Out_3(add3_21_out_3));
  Add3 add3_22 (
    .In0(add3_20_out_3), .In1(add3_23_out_0), .In2(add3_23_out_1), .In3(add3_23_out_2),
    .Out_0(add3_22_out_0), .Out_1(add3_22_out_1), .Out_2(add3_22_out_2), .Out_3(add3_22_out_3));
  Add3 add3_23 (
    .In0(add3_21_out_3), .In1(add3_24_out_0), .In2(add3_24_out_1), .In3(add3_24_out_2),
    .Out_0(add3_23_out_0), .Out_1(add3_23_out_1), .Out_2(add3_23_out_2), .Out_3(add3_23_out_3));
  Add3 add3_24 (
    .In0(add3_10_out_3), .In1(add3_13_out_0), .In2(add3_13_out_1), .In3(add3_13_out_2),
    .Out_0(add3_24_out_0), .Out_1(add3_24_out_1), .Out_2(add3_24_out_2), .Out_3(add3_24_out_3));
  Add3 add3_25 (
    .In0(add3_23_out_3), .In1(add3_26_out_0), .In2(add3_26_out_1), .In3(add3_26_out_2),
    .Out_0(add3_25_out_0), .Out_1(add3_25_out_1), .Out_2(add3_25_out_2), .Out_3(add3_25_out_3));
  Add3 add3_26 (
    .In0(add3_24_out_3), .In1(add3_27_out_0), .In2(add3_27_out_1), .In3(add3_27_out_2),
    .Out_0(add3_26_out_0), .Out_1(add3_26_out_1), .Out_2(add3_26_out_2), .Out_3(add3_26_out_3));
  Add3 add3_27 (
    .In0(add3_13_out_3), .In1(add3_16_out_0), .In2(add3_16_out_1), .In3(add3_16_out_2),
    .Out_0(add3_27_out_0), .Out_1(add3_27_out_1), .Out_2(add3_27_out_2), .Out_3(add3_27_out_3));
  Add3 add3_28 (
    .In0(add3_26_out_3), .In1(add3_29_out_0), .In2(add3_29_out_1), .In3(add3_29_out_2),
    .Out_0(add3_28_out_0), .Out_1(add3_28_out_1), .Out_2(add3_28_out_2), .Out_3(add3_28_out_3));
  Add3 add3_29 (
    .In0(add3_27_out_3), .In1(add3_30_out_0), .In2(add3_30_out_1), .In3(add3_30_out_2),
    .Out_0(add3_29_out_0), .Out_1(add3_29_out_1), .Out_2(add3_29_out_2), .Out_3(add3_29_out_3));
  Add3 add3_30 (
    .In0(add3_16_out_3), .In1(add3_17_out_3), .In2(add3_18_out_3), .In3(1'b0), .Out_0(add3_30_out_0),
    .Out_1(add3_30_out_1), .Out_2(add3_30_out_2), .Out_3(add3_30_out_3));
  Add3 add3_31 (
    .In0(In[16]), .In1(add3_32_out_0), .In2(add3_32_out_1), .In3(add3_32_out_2), .Out_0(add3_31_out_0),
    .Out_1(add3_31_out_1), .Out_2(add3_31_out_2), .Out_3(add3_31_out_3));
  Add3 add3_32 (
    .In0(In[17]), .In1(add3_19_out_0), .In2(add3_19_out_1), .In3(add3_19_out_2), .Out_0(add3_32_out_0),
    .Out_1(add3_32_out_1), .Out_2(add3_32_out_2), .Out_3(add3_32_out_3));
  Add3 add3_33 (
    .In0(add3_32_out_3), .In1(add3_34_out_0), .In2(add3_34_out_1), .In3(add3_34_out_2),
    .Out_0(add3_33_out_0), .Out_1(add3_33_out_1), .Out_2(add3_33_out_2), .Out_3(add3_33_out_3));
  Add3 add3_34 (
    .In0(add3_19_out_3), .In1(add3_22_out_0), .In2(add3_22_out_1), .In3(add3_22_out_2),
    .Out_0(add3_34_out_0), .Out_1(add3_34_out_1), .Out_2(add3_34_out_2), .Out_3(add3_34_out_3));
  Add3 add3_35 (
    .In0(add3_34_out_3), .In1(add3_36_out_0), .In2(add3_36_out_1), .In3(add3_36_out_2),
    .Out_0(add3_35_out_0), .Out_1(add3_35_out_1), .Out_2(add3_35_out_2), .Out_3(add3_35_out_3));
  Add3 add3_36 (
    .In0(add3_22_out_3), .In1(add3_25_out_0), .In2(add3_25_out_1), .In3(add3_25_out_2),
    .Out_0(add3_36_out_0), .Out_1(add3_36_out_1), .Out_2(add3_36_out_2), .Out_3(add3_36_out_3));
  Add3 add3_37 (
    .In0(add3_36_out_3), .In1(add3_38_out_0), .In2(add3_38_out_1), .In3(add3_38_out_2),
    .Out_0(add3_37_out_0), .Out_1(add3_37_out_1), .Out_2(add3_37_out_2), .Out_3(add3_37_out_3));
  Add3 add3_38 (
    .In0(add3_25_out_3), .In1(add3_28_out_0), .In2(add3_28_out_1), .In3(add3_28_out_2),
    .Out_0(add3_38_out_0), .Out_1(add3_38_out_1), .Out_2(add3_38_out_2), .Out_3(add3_38_out_3));
  Add3 add3_39 (
    .In0(add3_38_out_3), .In1(add3_40_out_0), .In2(add3_40_out_1), .In3(add3_40_out_2),
    .Out_0(add3_39_out_0), .Out_1(add3_39_out_1), .Out_2(add3_39_out_2), .Out_3(add3_39_out_3));
  Add3 add3_40 (
    .In0(add3_28_out_3), .In1(add3_29_out_3), .In2(add3_30_out_3), .In3(1'b0), .Out_0(add3_40_out_0),
    .Out_1(add3_40_out_1), .Out_2(add3_40_out_2), .Out_3(add3_40_out_3));
  Add3 add3_41 (
    .In0(In[13]), .In1(add3_42_out_0), .In2(add3_42_out_1), .In3(add3_42_out_2), .Out_0(add3_41_out_0),
    .Out_1(add3_41_out_1), .Out_2(add3_41_out_2), .Out_3(add3_41_out_3));
  Add3 add3_42 (
    .In0(In[14]), .In1(add3_43_out_0), .In2(add3_43_out_1), .In3(add3_43_out_2), .Out_0(add3_42_out_0),
    .Out_1(add3_42_out_1), .Out_2(add3_42_out_2), .Out_3(add3_42_out_3));
  Add3 add3_43 (
    .In0(In[15]), .In1(add3_31_out_0), .In2(add3_31_out_1), .In3(add3_31_out_2), .Out_0(add3_43_out_0),
    .Out_1(add3_43_out_1), .Out_2(add3_43_out_2), .Out_3(add3_43_out_3));
  Add3 add3_44 (
    .In0(add3_42_out_3), .In1(add3_45_out_0), .In2(add3_45_out_1), .In3(add3_45_out_2),
    .Out_0(add3_44_out_0), .Out_1(add3_44_out_1), .Out_2(add3_44_out_2), .Out_3(add3_44_out_3));
  Add3 add3_45 (
    .In0(add3_43_out_3), .In1(add3_46_out_0), .In2(add3_46_out_1), .In3(add3_46_out_2),
    .Out_0(add3_45_out_0), .Out_1(add3_45_out_1), .Out_2(add3_45_out_2), .Out_3(add3_45_out_3));
  Add3 add3_46 (
    .In0(add3_31_out_3), .In1(add3_33_out_0), .In2(add3_33_out_1), .In3(add3_33_out_2),
    .Out_0(add3_46_out_0), .Out_1(add3_46_out_1), .Out_2(add3_46_out_2), .Out_3(add3_46_out_3));
  Add3 add3_47 (
    .In0(add3_45_out_3), .In1(add3_48_out_0), .In2(add3_48_out_1), .In3(add3_48_out_2),
    .Out_0(add3_47_out_0), .Out_1(add3_47_out_1), .Out_2(add3_47_out_2), .Out_3(add3_47_out_3));
  Add3 add3_48 (
    .In0(add3_46_out_3), .In1(add3_49_out_0), .In2(add3_49_out_1), .In3(add3_49_out_2),
    .Out_0(add3_48_out_0), .Out_1(add3_48_out_1), .Out_2(add3_48_out_2), .Out_3(add3_48_out_3));
  Add3 add3_49 (
    .In0(add3_33_out_3), .In1(add3_35_out_0), .In2(add3_35_out_1), .In3(add3_35_out_2),
    .Out_0(add3_49_out_0), .Out_1(add3_49_out_1), .Out_2(add3_49_out_2), .Out_3(add3_49_out_3));
  Add3 add3_50 (
    .In0(add3_48_out_3), .In1(add3_51_out_0), .In2(add3_51_out_1), .In3(add3_51_out_2),
    .Out_0(add3_50_out_0), .Out_1(add3_50_out_1), .Out_2(add3_50_out_2), .Out_3(add3_50_out_3));
  Add3 add3_51 (
    .In0(add3_49_out_3), .In1(add3_52_out_0), .In2(add3_52_out_1), .In3(add3_52_out_2),
    .Out_0(add3_51_out_0), .Out_1(add3_51_out_1), .Out_2(add3_51_out_2), .Out_3(add3_51_out_3));
  Add3 add3_52 (
    .In0(add3_35_out_3), .In1(add3_37_out_0), .In2(add3_37_out_1), .In3(add3_37_out_2),
    .Out_0(add3_52_out_0), .Out_1(add3_52_out_1), .Out_2(add3_52_out_2), .Out_3(add3_52_out_3));
  Add3 add3_53 (
    .In0(add3_51_out_3), .In1(add3_54_out_0), .In2(add3_54_out_1), .In3(add3_54_out_2),
    .Out_0(add3_53_out_0), .Out_1(add3_53_out_1), .Out_2(add3_53_out_2), .Out_3(add3_53_out_3));
  Add3 add3_54 (
    .In0(add3_52_out_3), .In1(add3_55_out_0), .In2(add3_55_out_1), .In3(add3_55_out_2),
    .Out_0(add3_54_out_0), .Out_1(add3_54_out_1), .Out_2(add3_54_out_2), .Out_3(add3_54_out_3));
  Add3 add3_55 (
    .In0(add3_37_out_3), .In1(add3_39_out_0), .In2(add3_39_out_1), .In3(add3_39_out_2),
    .Out_0(add3_55_out_0), .Out_1(add3_55_out_1), .Out_2(add3_55_out_2), .Out_3(add3_55_out_3));
  Add3 add3_56 (
    .In0(add3_54_out_3), .In1(add3_57_out_0), .In2(add3_57_out_1), .In3(add3_57_out_2),
    .Out_0(add3_56_out_0), .Out_1(add3_56_out_1), .Out_2(add3_56_out_2), .Out_3(add3_56_out_3));
  Add3 add3_57 (
    .In0(add3_55_out_3), .In1(add3_39_out_3), .In2(add3_40_out_3), .In3(1'b0), .Out_0(add3_57_out_0),
    .Out_1(add3_57_out_1), .Out_2(add3_57_out_2), .Out_3(add3_57_out_3));
  Add3 add3_58 (
    .In0(In[10]), .In1(add3_59_out_0), .In2(add3_59_out_1), .In3(add3_59_out_2), .Out_0(add3_58_out_0),
    .Out_1(add3_58_out_1), .Out_2(add3_58_out_2), .Out_3(add3_58_out_3));
  Add3 add3_59 (
    .In0(In[11]), .In1(add3_60_out_0), .In2(add3_60_out_1), .In3(add3_60_out_2), .Out_0(add3_59_out_0),
    .Out_1(add3_59_out_1), .Out_2(add3_59_out_2), .Out_3(add3_59_out_3));
  Add3 add3_60 (
    .In0(In[12]), .In1(add3_41_out_0), .In2(add3_41_out_1), .In3(add3_41_out_2), .Out_0(add3_60_out_0),
    .Out_1(add3_60_out_1), .Out_2(add3_60_out_2), .Out_3(add3_60_out_3));
  Add3 add3_61 (
    .In0(add3_59_out_3), .In1(add3_62_out_0), .In2(add3_62_out_1), .In3(add3_62_out_2),
    .Out_0(add3_61_out_0), .Out_1(add3_61_out_1), .Out_2(add3_61_out_2), .Out_3(add3_61_out_3));
  Add3 add3_62 (
    .In0(add3_60_out_3), .In1(add3_63_out_0), .In2(add3_63_out_1), .In3(add3_63_out_2),
    .Out_0(add3_62_out_0), .Out_1(add3_62_out_1), .Out_2(add3_62_out_2), .Out_3(add3_62_out_3));
  Add3 add3_63 (
    .In0(add3_41_out_3), .In1(add3_44_out_0), .In2(add3_44_out_1), .In3(add3_44_out_2),
    .Out_0(add3_63_out_0), .Out_1(add3_63_out_1), .Out_2(add3_63_out_2), .Out_3(add3_63_out_3));
  Add3 add3_64 (
    .In0(add3_62_out_3), .In1(add3_65_out_0), .In2(add3_65_out_1), .In3(add3_65_out_2),
    .Out_0(add3_64_out_0), .Out_1(add3_64_out_1), .Out_2(add3_64_out_2), .Out_3(add3_64_out_3));
  Add3 add3_65 (
    .In0(add3_63_out_3), .In1(add3_66_out_0), .In2(add3_66_out_1), .In3(add3_66_out_2),
    .Out_0(add3_65_out_0), .Out_1(add3_65_out_1), .Out_2(add3_65_out_2), .Out_3(add3_65_out_3));
  Add3 add3_66 (
    .In0(add3_44_out_3), .In1(add3_47_out_0), .In2(add3_47_out_1), .In3(add3_47_out_2),
    .Out_0(add3_66_out_0), .Out_1(add3_66_out_1), .Out_2(add3_66_out_2), .Out_3(add3_66_out_3));
  Add3 add3_67 (
    .In0(add3_65_out_3), .In1(add3_68_out_0), .In2(add3_68_out_1), .In3(add3_68_out_2),
    .Out_0(add3_67_out_0), .Out_1(add3_67_out_1), .Out_2(add3_67_out_2), .Out_3(add3_67_out_3));
  Add3 add3_68 (
    .In0(add3_66_out_3), .In1(add3_69_out_0), .In2(add3_69_out_1), .In3(add3_69_out_2),
    .Out_0(add3_68_out_0), .Out_1(add3_68_out_1), .Out_2(add3_68_out_2), .Out_3(add3_68_out_3));
  Add3 add3_69 (
    .In0(add3_47_out_3), .In1(add3_50_out_0), .In2(add3_50_out_1), .In3(add3_50_out_2),
    .Out_0(add3_69_out_0), .Out_1(add3_69_out_1), .Out_2(add3_69_out_2), .Out_3(add3_69_out_3));
  Add3 add3_70 (
    .In0(add3_68_out_3), .In1(add3_71_out_0), .In2(add3_71_out_1), .In3(add3_71_out_2),
    .Out_0(add3_70_out_0), .Out_1(add3_70_out_1), .Out_2(add3_70_out_2), .Out_3(add3_70_out_3));
  Add3 add3_71 (
    .In0(add3_69_out_3), .In1(add3_72_out_0), .In2(add3_72_out_1), .In3(add3_72_out_2),
    .Out_0(add3_71_out_0), .Out_1(add3_71_out_1), .Out_2(add3_71_out_2), .Out_3(add3_71_out_3));
  Add3 add3_72 (
    .In0(add3_50_out_3), .In1(add3_53_out_0), .In2(add3_53_out_1), .In3(add3_53_out_2),
    .Out_0(add3_72_out_0), .Out_1(add3_72_out_1), .Out_2(add3_72_out_2), .Out_3(add3_72_out_3));
  Add3 add3_73 (
    .In0(add3_71_out_3), .In1(add3_74_out_0), .In2(add3_74_out_1), .In3(add3_74_out_2),
    .Out_0(add3_73_out_0), .Out_1(add3_73_out_1), .Out_2(add3_73_out_2), .Out_3(add3_73_out_3));
  Add3 add3_74 (
    .In0(add3_72_out_3), .In1(add3_75_out_0), .In2(add3_75_out_1), .In3(add3_75_out_2),
    .Out_0(add3_74_out_0), .Out_1(add3_74_out_1), .Out_2(add3_74_out_2), .Out_3(add3_74_out_3));
  Add3 add3_75 (
    .In0(add3_53_out_3), .In1(add3_56_out_0), .In2(add3_56_out_1), .In3(add3_56_out_2),
    .Out_0(add3_75_out_0), .Out_1(add3_75_out_1), .Out_2(add3_75_out_2), .Out_3(add3_75_out_3));
  Add3 add3_76 (
    .In0(add3_74_out_3), .In1(add3_77_out_0), .In2(add3_77_out_1), .In3(add3_77_out_2),
    .Out_0(add3_76_out_0), .Out_1(add3_76_out_1), .Out_2(add3_76_out_2), .Out_3(add3_76_out_3));
  Add3 add3_77 (
    .In0(add3_75_out_3), .In1(add3_56_out_3), .In2(add3_57_out_3), .In3(1'b0), .Out_0(add3_77_out_0),
    .Out_1(add3_77_out_1), .Out_2(add3_77_out_2), .Out_3(add3_77_out_3));
  Add3 add3_78 (
    .In0(In[8]), .In1(add3_79_out_0), .In2(add3_79_out_1), .In3(add3_79_out_2), .Out_0(add3_78_out_0),
    .Out_1(add3_78_out_1), .Out_2(add3_78_out_2), .Out_3(add3_78_out_3));
  Add3 add3_79 (
    .In0(In[9]), .In1(add3_58_out_0), .In2(add3_58_out_1), .In3(add3_58_out_2), .Out_0(add3_79_out_0),
    .Out_1(add3_79_out_1), .Out_2(add3_79_out_2), .Out_3(add3_79_out_3));
  Add3 add3_80 (
    .In0(add3_79_out_3), .In1(add3_81_out_0), .In2(add3_81_out_1), .In3(add3_81_out_2),
    .Out_0(add3_80_out_0), .Out_1(add3_80_out_1), .Out_2(add3_80_out_2), .Out_3(add3_80_out_3));
  Add3 add3_81 (
    .In0(add3_58_out_3), .In1(add3_61_out_0), .In2(add3_61_out_1), .In3(add3_61_out_2),
    .Out_0(add3_81_out_0), .Out_1(add3_81_out_1), .Out_2(add3_81_out_2), .Out_3(add3_81_out_3));
  Add3 add3_82 (
    .In0(add3_81_out_3), .In1(add3_83_out_0), .In2(add3_83_out_1), .In3(add3_83_out_2),
    .Out_0(add3_82_out_0), .Out_1(add3_82_out_1), .Out_2(add3_82_out_2), .Out_3(add3_82_out_3));
  Add3 add3_83 (
    .In0(add3_61_out_3), .In1(add3_64_out_0), .In2(add3_64_out_1), .In3(add3_64_out_2),
    .Out_0(add3_83_out_0), .Out_1(add3_83_out_1), .Out_2(add3_83_out_2), .Out_3(add3_83_out_3));
  Add3 add3_84 (
    .In0(add3_83_out_3), .In1(add3_85_out_0), .In2(add3_85_out_1), .In3(add3_85_out_2),
    .Out_0(add3_84_out_0), .Out_1(add3_84_out_1), .Out_2(add3_84_out_2), .Out_3(add3_84_out_3));
  Add3 add3_85 (
    .In0(add3_64_out_3), .In1(add3_67_out_0), .In2(add3_67_out_1), .In3(add3_67_out_2),
    .Out_0(add3_85_out_0), .Out_1(add3_85_out_1), .Out_2(add3_85_out_2), .Out_3(add3_85_out_3));
  Add3 add3_86 (
    .In0(add3_85_out_3), .In1(add3_87_out_0), .In2(add3_87_out_1), .In3(add3_87_out_2),
    .Out_0(add3_86_out_0), .Out_1(add3_86_out_1), .Out_2(add3_86_out_2), .Out_3(add3_86_out_3));
  Add3 add3_87 (
    .In0(add3_67_out_3), .In1(add3_70_out_0), .In2(add3_70_out_1), .In3(add3_70_out_2),
    .Out_0(add3_87_out_0), .Out_1(add3_87_out_1), .Out_2(add3_87_out_2), .Out_3(add3_87_out_3));
  Add3 add3_88 (
    .In0(add3_87_out_3), .In1(add3_89_out_0), .In2(add3_89_out_1), .In3(add3_89_out_2),
    .Out_0(add3_88_out_0), .Out_1(add3_88_out_1), .Out_2(add3_88_out_2), .Out_3(add3_88_out_3));
  Add3 add3_89 (
    .In0(add3_70_out_3), .In1(add3_73_out_0), .In2(add3_73_out_1), .In3(add3_73_out_2),
    .Out_0(add3_89_out_0), .Out_1(add3_89_out_1), .Out_2(add3_89_out_2), .Out_3(add3_89_out_3));
  Add3 add3_90 (
    .In0(add3_89_out_3), .In1(add3_91_out_0), .In2(add3_91_out_1), .In3(add3_91_out_2),
    .Out_0(add3_90_out_0), .Out_1(add3_90_out_1), .Out_2(add3_90_out_2), .Out_3(add3_90_out_3));
  Add3 add3_91 (
    .In0(add3_73_out_3), .In1(add3_76_out_0), .In2(add3_76_out_1), .In3(add3_76_out_2),
    .Out_0(add3_91_out_0), .Out_1(add3_91_out_1), .Out_2(add3_91_out_2), .Out_3(add3_91_out_3));
  Add3 add3_92 (
    .In0(add3_91_out_3), .In1(add3_76_out_3), .In2(add3_77_out_3), .In3(1'b0), .Out_0(add3_92_out_0),
    .Out_1(add3_92_out_1), .Out_2(add3_92_out_2), .Out_3(add3_92_out_3));
  Add3 add3_93 (
    .In0(In[5]), .In1(add3_94_out_0), .In2(add3_94_out_1), .In3(add3_94_out_2), .Out_0(add3_93_out_0),
    .Out_1(add3_93_out_1), .Out_2(add3_93_out_2), .Out_3(add3_93_out_3));
  Add3 add3_94 (
    .In0(In[6]), .In1(add3_95_out_0), .In2(add3_95_out_1), .In3(add3_95_out_2), .Out_0(add3_94_out_0),
    .Out_1(add3_94_out_1), .Out_2(add3_94_out_2), .Out_3(add3_94_out_3));
  Add3 add3_95 (
    .In0(In[7]), .In1(add3_78_out_0), .In2(add3_78_out_1), .In3(add3_78_out_2), .Out_0(add3_95_out_0),
    .Out_1(add3_95_out_1), .Out_2(add3_95_out_2), .Out_3(add3_95_out_3));
  Add3 add3_96 (
    .In0(add3_94_out_3), .In1(add3_97_out_0), .In2(add3_97_out_1), .In3(add3_97_out_2),
    .Out_0(add3_96_out_0), .Out_1(add3_96_out_1), .Out_2(add3_96_out_2), .Out_3(add3_96_out_3));
  Add3 add3_97 (
    .In0(add3_95_out_3), .In1(add3_98_out_0), .In2(add3_98_out_1), .In3(add3_98_out_2),
    .Out_0(add3_97_out_0), .Out_1(add3_97_out_1), .Out_2(add3_97_out_2), .Out_3(add3_97_out_3));
  Add3 add3_98 (
    .In0(add3_78_out_3), .In1(add3_80_out_0), .In2(add3_80_out_1), .In3(add3_80_out_2),
    .Out_0(add3_98_out_0), .Out_1(add3_98_out_1), .Out_2(add3_98_out_2), .Out_3(add3_98_out_3));
  Add3 add3_99 (
    .In0(add3_97_out_3), .In1(add3_100_out_0), .In2(add3_100_out_1), .In3(add3_100_out_2),
    .Out_0(add3_99_out_0), .Out_1(add3_99_out_1), .Out_2(add3_99_out_2), .Out_3(add3_99_out_3));
  Add3 add3_100 (
    .In0(add3_98_out_3), .In1(add3_101_out_0), .In2(add3_101_out_1), .In3(add3_101_out_2),
    .Out_0(add3_100_out_0), .Out_1(add3_100_out_1), .Out_2(add3_100_out_2), .Out_3(add3_100_out_3));
  Add3 add3_101 (
    .In0(add3_80_out_3), .In1(add3_82_out_0), .In2(add3_82_out_1), .In3(add3_82_out_2),
    .Out_0(add3_101_out_0), .Out_1(add3_101_out_1), .Out_2(add3_101_out_2), .Out_3(add3_101_out_3));
  Add3 add3_102 (
    .In0(add3_100_out_3), .In1(add3_103_out_0), .In2(add3_103_out_1), .In3(add3_103_out_2),
    .Out_0(add3_102_out_0), .Out_1(add3_102_out_1), .Out_2(add3_102_out_2), .Out_3(add3_102_out_3));
  Add3 add3_103 (
    .In0(add3_101_out_3), .In1(add3_104_out_0), .In2(add3_104_out_1), .In3(add3_104_out_2),
    .Out_0(add3_103_out_0), .Out_1(add3_103_out_1), .Out_2(add3_103_out_2), .Out_3(add3_103_out_3));
  Add3 add3_104 (
    .In0(add3_82_out_3), .In1(add3_84_out_0), .In2(add3_84_out_1), .In3(add3_84_out_2),
    .Out_0(add3_104_out_0), .Out_1(add3_104_out_1), .Out_2(add3_104_out_2), .Out_3(add3_104_out_3));
  Add3 add3_105 (
    .In0(add3_103_out_3), .In1(add3_106_out_0), .In2(add3_106_out_1), .In3(add3_106_out_2),
    .Out_0(add3_105_out_0), .Out_1(add3_105_out_1), .Out_2(add3_105_out_2), .Out_3(add3_105_out_3));
  Add3 add3_106 (
    .In0(add3_104_out_3), .In1(add3_107_out_0), .In2(add3_107_out_1), .In3(add3_107_out_2),
    .Out_0(add3_106_out_0), .Out_1(add3_106_out_1), .Out_2(add3_106_out_2), .Out_3(add3_106_out_3));
  Add3 add3_107 (
    .In0(add3_84_out_3), .In1(add3_86_out_0), .In2(add3_86_out_1), .In3(add3_86_out_2),
    .Out_0(add3_107_out_0), .Out_1(add3_107_out_1), .Out_2(add3_107_out_2), .Out_3(add3_107_out_3));
  Add3 add3_108 (
    .In0(add3_106_out_3), .In1(add3_109_out_0), .In2(add3_109_out_1), .In3(add3_109_out_2),
    .Out_0(add3_108_out_0), .Out_1(add3_108_out_1), .Out_2(add3_108_out_2), .Out_3(add3_108_out_3));
  Add3 add3_109 (
    .In0(add3_107_out_3), .In1(add3_110_out_0), .In2(add3_110_out_1), .In3(add3_110_out_2),
    .Out_0(add3_109_out_0), .Out_1(add3_109_out_1), .Out_2(add3_109_out_2), .Out_3(add3_109_out_3));
  Add3 add3_110 (
    .In0(add3_86_out_3), .In1(add3_88_out_0), .In2(add3_88_out_1), .In3(add3_88_out_2),
    .Out_0(add3_110_out_0), .Out_1(add3_110_out_1), .Out_2(add3_110_out_2), .Out_3(add3_110_out_3));
  Add3 add3_111 (
    .In0(add3_109_out_3), .In1(add3_112_out_0), .In2(add3_112_out_1), .In3(add3_112_out_2),
    .Out_0(add3_111_out_0), .Out_1(add3_111_out_1), .Out_2(add3_111_out_2), .Out_3(add3_111_out_3));
  Add3 add3_112 (
    .In0(add3_110_out_3), .In1(add3_113_out_0), .In2(add3_113_out_1), .In3(add3_113_out_2),
    .Out_0(add3_112_out_0), .Out_1(add3_112_out_1), .Out_2(add3_112_out_2), .Out_3(add3_112_out_3));
  Add3 add3_113 (
    .In0(add3_88_out_3), .In1(add3_90_out_0), .In2(add3_90_out_1), .In3(add3_90_out_2),
    .Out_0(add3_113_out_0), .Out_1(add3_113_out_1), .Out_2(add3_113_out_2), .Out_3(add3_113_out_3));
  Add3 add3_114 (
    .In0(add3_112_out_3), .In1(add3_115_out_0), .In2(add3_115_out_1), .In3(add3_115_out_2),
    .Out_0(add3_114_out_0), .Out_1(add3_114_out_1), .Out_2(add3_114_out_2), .Out_3(add3_114_out_3));
  Add3 add3_115 (
    .In0(add3_113_out_3), .In1(add3_116_out_0), .In2(add3_116_out_1), .In3(add3_116_out_2),
    .Out_0(add3_115_out_0), .Out_1(add3_115_out_1), .Out_2(add3_115_out_2), .Out_3(add3_115_out_3));
  Add3 add3_116 (
    .In0(add3_90_out_3), .In1(add3_92_out_0), .In2(add3_92_out_1), .In3(add3_92_out_2),
    .Out_0(add3_116_out_0), .Out_1(add3_116_out_1), .Out_2(add3_116_out_2), .Out_3(add3_116_out_3));
  Add3 add3_117 (
    .In0(add3_115_out_3), .In1(add3_116_out_3), .In2(add3_92_out_3), .In3(1'b0), .Out_0(add3_117_out_0),
    .Out_1(add3_117_out_1), .Out_2(add3_117_out_2), .Out_3(add3_117_out_3));
  Add3 add3_118 (
    .In0(In[2]), .In1(add3_119_out_0), .In2(add3_119_out_1), .In3(add3_119_out_2), .Out_0(add3_118_out_0),
    .Out_1(add3_118_out_1), .Out_2(add3_118_out_2), .Out_3(add3_118_out_3));
  Add3 add3_119 (
    .In0(In[3]), .In1(add3_120_out_0), .In2(add3_120_out_1), .In3(add3_120_out_2), .Out_0(add3_119_out_0),
    .Out_1(add3_119_out_1), .Out_2(add3_119_out_2), .Out_3(add3_119_out_3));
  Add3 add3_120 (
    .In0(In[4]), .In1(add3_93_out_0), .In2(add3_93_out_1), .In3(add3_93_out_2), .Out_0(add3_120_out_0),
    .Out_1(add3_120_out_1), .Out_2(add3_120_out_2), .Out_3(add3_120_out_3));
  Add3 add3_121 (
    .In0(add3_119_out_3), .In1(add3_122_out_0), .In2(add3_122_out_1), .In3(add3_122_out_2),
    .Out_0(add3_121_out_0), .Out_1(add3_121_out_1), .Out_2(add3_121_out_2), .Out_3(add3_121_out_3));
  Add3 add3_122 (
    .In0(add3_120_out_3), .In1(add3_123_out_0), .In2(add3_123_out_1), .In3(add3_123_out_2),
    .Out_0(add3_122_out_0), .Out_1(add3_122_out_1), .Out_2(add3_122_out_2), .Out_3(add3_122_out_3));
  Add3 add3_123 (
    .In0(add3_93_out_3), .In1(add3_96_out_0), .In2(add3_96_out_1), .In3(add3_96_out_2),
    .Out_0(add3_123_out_0), .Out_1(add3_123_out_1), .Out_2(add3_123_out_2), .Out_3(add3_123_out_3));
  Add3 add3_124 (
    .In0(add3_122_out_3), .In1(add3_125_out_0), .In2(add3_125_out_1), .In3(add3_125_out_2),
    .Out_0(add3_124_out_0), .Out_1(add3_124_out_1), .Out_2(add3_124_out_2), .Out_3(add3_124_out_3));
  Add3 add3_125 (
    .In0(add3_123_out_3), .In1(add3_126_out_0), .In2(add3_126_out_1), .In3(add3_126_out_2),
    .Out_0(add3_125_out_0), .Out_1(add3_125_out_1), .Out_2(add3_125_out_2), .Out_3(add3_125_out_3));
  Add3 add3_126 (
    .In0(add3_96_out_3), .In1(add3_99_out_0), .In2(add3_99_out_1), .In3(add3_99_out_2),
    .Out_0(add3_126_out_0), .Out_1(add3_126_out_1), .Out_2(add3_126_out_2), .Out_3(add3_126_out_3));
  Add3 add3_127 (
    .In0(add3_125_out_3), .In1(add3_128_out_0), .In2(add3_128_out_1), .In3(add3_128_out_2),
    .Out_0(add3_127_out_0), .Out_1(add3_127_out_1), .Out_2(add3_127_out_2), .Out_3(add3_127_out_3));
  Add3 add3_128 (
    .In0(add3_126_out_3), .In1(add3_129_out_0), .In2(add3_129_out_1), .In3(add3_129_out_2),
    .Out_0(add3_128_out_0), .Out_1(add3_128_out_1), .Out_2(add3_128_out_2), .Out_3(add3_128_out_3));
  Add3 add3_129 (
    .In0(add3_99_out_3), .In1(add3_102_out_0), .In2(add3_102_out_1), .In3(add3_102_out_2),
    .Out_0(add3_129_out_0), .Out_1(add3_129_out_1), .Out_2(add3_129_out_2), .Out_3(add3_129_out_3));
  Add3 add3_130 (
    .In0(add3_128_out_3), .In1(add3_131_out_0), .In2(add3_131_out_1), .In3(add3_131_out_2),
    .Out_0(add3_130_out_0), .Out_1(add3_130_out_1), .Out_2(add3_130_out_2), .Out_3(add3_130_out_3));
  Add3 add3_131 (
    .In0(add3_129_out_3), .In1(add3_132_out_0), .In2(add3_132_out_1), .In3(add3_132_out_2),
    .Out_0(add3_131_out_0), .Out_1(add3_131_out_1), .Out_2(add3_131_out_2), .Out_3(add3_131_out_3));
  Add3 add3_132 (
    .In0(add3_102_out_3), .In1(add3_105_out_0), .In2(add3_105_out_1), .In3(add3_105_out_2),
    .Out_0(add3_132_out_0), .Out_1(add3_132_out_1), .Out_2(add3_132_out_2), .Out_3(add3_132_out_3));
  Add3 add3_133 (
    .In0(add3_131_out_3), .In1(add3_134_out_0), .In2(add3_134_out_1), .In3(add3_134_out_2),
    .Out_0(add3_133_out_0), .Out_1(add3_133_out_1), .Out_2(add3_133_out_2), .Out_3(add3_133_out_3));
  Add3 add3_134 (
    .In0(add3_132_out_3), .In1(add3_135_out_0), .In2(add3_135_out_1), .In3(add3_135_out_2),
    .Out_0(add3_134_out_0), .Out_1(add3_134_out_1), .Out_2(add3_134_out_2), .Out_3(add3_134_out_3));
  Add3 add3_135 (
    .In0(add3_105_out_3), .In1(add3_108_out_0), .In2(add3_108_out_1), .In3(add3_108_out_2),
    .Out_0(add3_135_out_0), .Out_1(add3_135_out_1), .Out_2(add3_135_out_2), .Out_3(add3_135_out_3));
  Add3 add3_136 (
    .In0(add3_134_out_3), .In1(add3_137_out_0), .In2(add3_137_out_1), .In3(add3_137_out_2),
    .Out_0(add3_136_out_0), .Out_1(add3_136_out_1), .Out_2(add3_136_out_2), .Out_3(add3_136_out_3));
  Add3 add3_137 (
    .In0(add3_135_out_3), .In1(add3_138_out_0), .In2(add3_138_out_1), .In3(add3_138_out_2),
    .Out_0(add3_137_out_0), .Out_1(add3_137_out_1), .Out_2(add3_137_out_2), .Out_3(add3_137_out_3));
  Add3 add3_138 (
    .In0(add3_108_out_3), .In1(add3_111_out_0), .In2(add3_111_out_1), .In3(add3_111_out_2),
    .Out_0(add3_138_out_0), .Out_1(add3_138_out_1), .Out_2(add3_138_out_2), .Out_3(add3_138_out_3));
  Add3 add3_139 (
    .In0(add3_137_out_3), .In1(add3_140_out_0), .In2(add3_140_out_1), .In3(add3_140_out_2),
    .Out_0(add3_139_out_0), .Out_1(add3_139_out_1), .Out_2(add3_139_out_2), .Out_3(add3_139_out_3));
  Add3 add3_140 (
    .In0(add3_138_out_3), .In1(add3_141_out_0), .In2(add3_141_out_1), .In3(add3_141_out_2),
    .Out_0(add3_140_out_0), .Out_1(add3_140_out_1), .Out_2(add3_140_out_2), .Out_3(add3_140_out_3));
  Add3 add3_141 (
    .In0(add3_111_out_3), .In1(add3_114_out_0), .In2(add3_114_out_1), .In3(add3_114_out_2),
    .Out_0(add3_141_out_0), .Out_1(add3_141_out_1), .Out_2(add3_141_out_2), .Out_3(add3_141_out_3));
  Add3 add3_142 (
    .In0(add3_140_out_3), .In1(add3_143_out_0), .In2(add3_143_out_1), .In3(add3_143_out_2),
    .Out_0(add3_142_out_0), .Out_1(add3_142_out_1), .Out_2(add3_142_out_2), .Out_3(add3_142_out_3));
  Add3 add3_143 (
    .In0(add3_141_out_3), .In1(add3_144_out_0), .In2(add3_144_out_1), .In3(add3_144_out_2),
    .Out_0(add3_143_out_0), .Out_1(add3_143_out_1), .Out_2(add3_143_out_2), .Out_3(add3_143_out_3));
  Add3 add3_144 (
    .In0(add3_114_out_3), .In1(add3_117_out_0), .In2(add3_117_out_1), .In3(add3_117_out_2),
    .Out_0(add3_144_out_0), .Out_1(add3_144_out_1), .Out_2(add3_144_out_2), .Out_3(add3_144_out_3));
  Add3 add3_145 (
    .In0(add3_143_out_3), .In1(add3_144_out_3), .In2(add3_117_out_3), .In3(1'b0), .Out_0(add3_145_out_0),
    .Out_1(add3_145_out_1), .Out_2(add3_145_out_2));  // open: Out_3
  Add3 add3_146 (
    .In0(In[1]), .In1(add3_118_out_0), .In2(add3_118_out_1), .In3(add3_118_out_2), .Out_0(add3_146_out_0[1]),
    .Out_1(add3_146_out_0[2]), .Out_2(add3_146_out_0[3]), .Out_3(add3_146_out_3[0]));
  Add3 add3_147 (
    .In0(add3_118_out_3), .In1(add3_121_out_0), .In2(add3_121_out_1), .In3(add3_121_out_2),
    .Out_0(add3_146_out_3[1]), .Out_1(add3_146_out_3[2]), .Out_2(add3_146_out_3[3]), .Out_3(add3_147_out_3[0]));
  Add3 add3_148 (
    .In0(add3_121_out_3), .In1(add3_124_out_0), .In2(add3_124_out_1), .In3(add3_124_out_2),
    .Out_0(add3_147_out_3[1]), .Out_1(add3_147_out_3[2]), .Out_2(add3_147_out_3[3]), .Out_3(add3_148_out_3[0]));
  Add3 add3_149 (
    .In0(add3_124_out_3), .In1(add3_127_out_0), .In2(add3_127_out_1), .In3(add3_127_out_2),
    .Out_0(add3_148_out_3[1]), .Out_1(add3_148_out_3[2]), .Out_2(add3_148_out_3[3]), .Out_3(add3_149_out_3[0]));
  Add3 add3_150 (
    .In0(add3_127_out_3), .In1(add3_130_out_0), .In2(add3_130_out_1), .In3(add3_130_out_2),
    .Out_0(add3_149_out_3[1]), .Out_1(add3_149_out_3[2]), .Out_2(add3_149_out_3[3]), .Out_3(add3_150_out_3[0]));
  Add3 add3_151 (
    .In0(add3_130_out_3), .In1(add3_133_out_0), .In2(add3_133_out_1), .In3(add3_133_out_2),
    .Out_0(add3_150_out_3[1]), .Out_1(add3_150_out_3[2]), .Out_2(add3_150_out_3[3]), .Out_3(add3_151_out_3[0]));
  Add3 add3_152 (
    .In0(add3_133_out_3), .In1(add3_136_out_0), .In2(add3_136_out_1), .In3(add3_136_out_2),
    .Out_0(add3_151_out_3[1]), .Out_1(add3_151_out_3[2]), .Out_2(add3_151_out_3[3]), .Out_3(add3_152_out_3[0]));
  Add3 add3_153 (
    .In0(add3_136_out_3), .In1(add3_139_out_0), .In2(add3_139_out_1), .In3(add3_139_out_2),
    .Out_0(add3_152_out_3[1]), .Out_1(add3_152_out_3[2]), .Out_2(add3_152_out_3[3]), .Out_3(add3_153_out_3[0]));
  Add3 add3_154 (
    .In0(add3_139_out_3), .In1(add3_142_out_0), .In2(add3_142_out_1), .In3(add3_142_out_2),
    .Out_0(add3_153_out_3[1]), .Out_1(add3_153_out_3[2]), .Out_2(add3_153_out_3[3]), .Out_3(add3_154_out_3[0]));
  Add3 add3_155 (
    .In0(add3_142_out_3), .In1(add3_145_out_0), .In2(add3_145_out_1), .In3(add3_145_out_2),
    .Out_0(add3_154_out_3[1]), .Out_1(add3_154_out_3[2]), .Out_2(add3_154_out_3[3]));  // open: Out_3
  HexToAscii hextoascii_1 (.In({add3_146_out_0, In[0]}), .Out(_1));
  HexToAscii hextoascii_2 (.In(add3_146_out_3), .Out(_10));
  HexToAscii hextoascii_3 (.In(add3_147_out_3), .Out(_100));
  HexToAscii hextoascii_4 (.In(add3_148_out_3), .Out(_1_000));
  HexToAscii hextoascii_5 (.In(add3_149_out_3), .Out(_10_000));
  HexToAscii hextoascii_6 (.In(add3_150_out_3), .Out(_100_000));
  HexToAscii hextoascii_7 (.In(add3_151_out_3), .Out(_1_000_000));
  HexToAscii hextoascii_8 (.In(add3_152_out_3), .Out(_10_000_000));
  HexToAscii hextoascii_9 (.In(add3_153_out_3), .Out(_100_000_000));
  HexToAscii hextoascii_10 (.In(add3_154_out_3), .Out(_1_000_000_000));
endmodule

// +3If>4
module Add3 (
  input  In0,
  input  In1,
  input  In2,
  input  In3,
  output Out_0,
  output Out_1,
  output Out_2,
  output Out_3
);

  wire comparator_1_gt, not_1_out;
  wire [3:0] adder_1_out;

  Comparator #(.width(4), .mode("unsigned")) comparator_1 (
    .a({In3, In2, In1, In0}), .b(4'b0100), .gt(comparator_1_gt));  // open: eq, lt
  assign {Out_3, Out_2, Out_1, Out_0} = not_1_out ? {In3, In2, In1, In0} : 4'bz;  // Controlled_Buffer controlled_buffer_1
  not not_1 (not_1_out, comparator_1_gt);
  Adder #(.width(4)) adder_1 (.a({In3, In2, In1, In0}), .b(4'b0011), .out(adder_1_out));  // open: cin, cout
  assign {Out_3, Out_2, Out_1, Out_0} = comparator_1_gt ? adder_1_out : 4'bz;  // Controlled_Buffer controlled_buffer_2
endmodule

module HexToAscii (
  input  [3:0] In,
  output [6:0] Out
);

  wire equals_1_out, equals_2_out, equals_3_out, equals_4_out, equals_5_out, equals_6_out, equals_7_out,
       equals_8_out, equals_9_out, equals_10_out;
  wire [7:0] bit_extender_1_out;

  assign bit_extender_1_out = {{4{1'b0}}, In};  // Bit_Extender bit_extender_1
  assign Out = equals_1_out ? 7'b0110000 : 7'bz;  // Controlled_Buffer controlled_buffer_1
  equals equals_1 (.A(bit_extender_1_out), .B({8{1'b0}}), .Out(equals_1_out));
  assign Out = equals_2_out ? 7'b0110001 : 7'bz;  // Controlled_Buffer controlled_buffer_2
  equals equals_2 (.A(bit_extender_1_out), .B(8'h1), .Out(equals_2_out));
  assign Out = equals_3_out ? 7'b0110010 : 7'bz;  // Controlled_Buffer controlled_buffer_3
  equals equals_3 (.A(bit_extender_1_out), .B(8'h2), .Out(equals_3_out));
  assign Out = equals_4_out ? 7'b0110011 : 7'bz;  // Controlled_Buffer controlled_buffer_4
  equals equals_4 (.A(bit_extender_1_out), .B(8'h3), .Out(equals_4_out));
  assign Out = equals_5_out ? 7'b0110100 : 7'bz;  // Controlled_Buffer controlled_buffer_5
  equals equals_5 (.A(bit_extender_1_out), .B(8'h4), .Out(equals_5_out));
  assign Out = equals_6_out ? 7'b0110101 : 7'bz;  // Controlled_Buffer controlled_buffer_6
  equals equals_6 (.A(bit_extender_1_out), .B(8'h5), .Out(equals_6_out));
  assign Out = equals_7_out ? 7'b0110110 : 7'bz;  // Controlled_Buffer controlled_buffer_7
  equals equals_7 (.A(bit_extender_1_out), .B(8'h6), .Out(equals_7_out));
  assign Out = equals_8_out ? 7'b0110111 : 7'bz;  // Controlled_Buffer controlled_buffer_8
  equals equals_8 (.A(bit_extender_1_out), .B(8'h7), .Out(equals_8_out));
  assign Out = equals_9_out ? 7'b0111000 : 7'bz;  // Controlled_Buffer controlled_buffer_9
  equals equals_9 (.A(bit_extender_1_out), .B(8'h8), .Out(equals_9_out));
  assign Out = equals_10_out ? 7'b0111001 : 7'bz;  // Controlled_Buffer controlled_buffer_10
  equals equals_10 (.A(bit_extender_1_out), .B(8'h9), .Out(equals_10_out));
endmodule

// CMY
module LedMatrixDriver (
  input  [7:0] ImageNum,
  input  Clk,
  output [31:0] Red_Columns,
  output [31:0] Red_Rows,
  output [31:0] Green_Columns,
  output [31:0] Green_Rows,
  output [31:0] Blue_Columns,
  output [31:0] Blue_Rows,
  output [31:0] Loading_Columns,
  output [31:0] Loading_Rows
);

  wire comparator_1_eq, comparator_2_eq, comparator_3_eq, counter_2_carry, counter_4_carry, counter_9_q,
       counter_10_carry, demultiplexer_1_out0, demultiplexer_1_out1, demultiplexer_1_out2,
       demultiplexer_1_out3, demultiplexer_1_out4, demultiplexer_1_out5, nCLK, not_2_out, not_3_out,
       not_4_out, not_5_out, or_1_p2, Reset, ShowLoadingIcon;
  wire [2:0] counter_8_q;
  wire [7:0] register_1_q;
  wire [23:0] adder_1_out, adder_2_out, bit_extender_1_out, counter_1_q, counter_3_q, counter_7_q,
       multiplier_1_out, multiplier_2_out, subtractor_1_out;
  wire [31:0] Loading, register_8_q, register_9_q, rom_1_data;

  not not_1 (nCLK, Clk);
  Counter #(.width(24), .max('hffffff)) counter_1 (
    .count(1'b1), .Q(counter_1_q), .clk(Clk), .clr(Reset));  // open: load, D, carry
  Register register_1 (.D(ImageNum), .Q(register_1_q), .clk(nCLK));  // open: en, clr
  assign bit_extender_1_out = {{16{1'b0}}, ImageNum};  // Bit_Extender bit_extender_1
  Subtractor #(.width(24)) subtractor_1 (.a(counter_1_q), .b(24'h5), .out(subtractor_1_out));  // open: bin, bout
  Comparator #(.mode("unsigned")) comparator_1 (.a(register_1_q), .b(ImageNum), .eq(comparator_1_eq));  // open: gt, lt
  Counter #(.width(2), .max('h2), .ongoal("stay")) counter_2 (
    .count(1'b1), .carry(counter_2_carry), .clk(Reset), .clr(not_2_out));  // open: load, D, Q
  Multiplier #(.width(24)) multiplier_1 (
    .a(bit_extender_1_out), .b(24'h157c), .out(multiplier_1_out));  // open: cin, cout
  not not_2 (not_2_out, comparator_1_eq);
  Adder #(.width(24)) adder_1 (.a(multiplier_1_out), .b(subtractor_1_out), .out(adder_1_out));  // open: cin, cout
  S_R_Flip_Flop #(.trigger("falling")) s_r_ff_1 (
    .S(not_2_out), .clk(Clk), .R(counter_2_carry), .Q(ShowLoadingIcon));  // open: Qn, preset, reset, en
  ROM #(.addrWidth(24), .dataWidth(32)) rom_1 (.addr(adder_1_out), .data(rom_1_data));  // open: sel
  Counter #(.width(24), .max('hffffff)) counter_3 (
    .count(1'b1), .Q(counter_3_q), .clk(counter_4_carry), .clr(counter_10_carry));  // open: load, D, carry
  Counter #(.max('h3)) counter_4 (
    .count(comparator_3_eq), .carry(counter_4_carry), .clk(comparator_3_eq), .clr(counter_10_carry));  // open: load, D, Q
  Counter counter_5 ();  // open: load, D, count, Q, carry, clk, clr
  Comparator #(.width(32), .mode("unsigned")) comparator_2 (
    .a(rom_1_data), .b({32{1'b0}}), .eq(comparator_2_eq));  // open: gt, lt
  not not_3 (not_3_out, comparator_2_eq);
  Counter #(.width(6), .max('h3f)) counter_6 (
    .count(comparator_2_eq), .carry(Reset), .clk(Clk), .clr(or_1_p2));  // open: load, D, Q
  // OR_Gate or_1: pin names not known; wires that end beside it: not_3_out, or_1_p2, Reset
  Multiplier #(.width(24)) multiplier_2 (.a(counter_3_q), .b(24'h1000), .out(multiplier_2_out));  // open: cin, cout
  Counter #(.width(24), .max('hffffff)) counter_7 (
    .count(1'b1), .Q(counter_7_q), .clk(Clk), .clr(comparator_3_eq));  // open: load, D, carry
  Demultiplexer #(.select(3), .disabled(0), .enable("false")) demultiplexer_1 (
    .out0(demultiplexer_1_out0), .out1(demultiplexer_1_out1), .out2(demultiplexer_1_out2),
    .out3(demultiplexer_1_out3), .out4(demultiplexer_1_out4), .out5(demultiplexer_1_out5), .in(1'b1),
    .sel(counter_8_q));  // open: out6, out7
  Counter #(.width(3), .max('h5)) counter_8 (
    .count(1'b1), .Q(counter_8_q), .clk(Clk), .clr(Reset));  // open: load, D, carry
  Adder #(.width(24)) adder_2 (.a(multiplier_2_out), .b(counter_7_q), .out(adder_2_out));  // open: cin, cout
  ROM #(.addrWidth(24), .dataWidth(32)) rom_2 (.addr(adder_2_out), .data(Loading));  // open: sel
  Comparator #(.width(32), .mode("unsigned")) comparator_3 (
    .a(Loading), .b({32{1'b0}}), .eq(comparator_3_eq));  // open: gt, lt
  Counter #(.width(1), .max('h1)) counter_9 (
    .count(1'b1), .Q(counter_9_q), .clk(Clk), .clr(comparator_3_eq));  // open: load, D, carry
  Counter #(.max('h5)) counter_10 (
    .count(comparator_3_eq), .carry(counter_10_carry), .clk(Clk), .clr(not_4_out));  // open: load, D, Q
  not not_4 (not_4_out, comparator_3_eq);
  Register #(.width(32)) register_2 (
    .D(rom_1_data), .en(1'b1), .Q(Red_Columns), .clk(demultiplexer_1_out0));  // open: clr
  Register #(.width(32)) register_3 (.D(rom_1_data), .en(1'b1), .Q(Red_Rows), .clk(demultiplexer_1_out1));  // open: clr
  Register #(.width(32)) register_4 (
    .D(rom_1_data), .en(1'b1), .Q(Green_Columns), .clk(demultiplexer_1_out2));  // open: clr
  Register #(.width(32)) register_5 (
    .D(rom_1_data), .en(1'b1), .Q(Green_Rows), .clk(demultiplexer_1_out3));  // open: clr
  Register #(.width(32)) register_6 (
    .D(rom_1_data), .en(1'b1), .Q(Blue_Columns), .clk(demultiplexer_1_out4));  // open: clr
  Register #(.width(32)) register_7 (
    .D(rom_1_data), .en(1'b1), .Q(Blue_Rows), .clk(demultiplexer_1_out5));  // open: clr
  Register #(.width(32)) register_8 (.D(Loading), .en(1'b1), .Q(register_8_q), .clk(counter_9_q));  // open: clr
  Register #(.width(32)) register_9 (.D(Loading), .en(1'b1), .Q(register_9_q), .clk(not_5_out));  // open: clr
  not not_5 (not_5_out, counter_9_q);
  assign Loading_Columns = ShowLoadingIcon ? register_8_q : 32'bz;  // Controlled_Buffer controlled_buffer_1
  Pull_Resistor pull_resistor_1 (.node(Loading_Columns));
  assign Loading_Rows = ShowLoadingIcon ? register_9_q : 32'bz;  // Controlled_Buffer controlled_buffer_2
  Pull_Resistor pull_resistor_2 (.node(Loading_Rows));

  // Notes on the sheet:
  //   Images
  //   Column
  //   contents of rom_1 (hex, n*v repeats v):
  //   0 0 40000 4000000 400 40000000 0 0 80000 4000000 800 40000000 0 0 100000 4000000 1000 40000000 0 0
  //   40000 2000000 2000 40000000 0 0 80000 2000000 4000 40000000 0 0 100000 2000000 8000 40000000 0 0
  //   40000 1000000 10000 40000000 0 0 80000 1000000 20000 40000000 0 0 100000 1000000 40000 40000000 4*0
  //   80000 40000000 4*0 100000 40000000 4*0 200000 40000000 4*0 100 20000000 4*0 200 20000000 4*0 400
  //   20000000 4*0 800 20000000 4*0 1000 20000000 4*0 2000 20000000 4*0 4000 20000000 4*0 8000 20000000
  //   4*0 10000 20000000 4*0 20000 20000000 4*0 40000 20000000 4*0 80000 20000000 4*0 100000 20000000 4*0
  //   200000 20000000 4*0 400000 20000000 4*0 800000 20000000 4*0 80 10000000 4*0 100 10000000 4*0 200
  //   10000000 4*0 400 10000000 4*0 800 10000000 4*0 1000 10000000 4*0 2000 10000000 4*0 4000 10000000 4*0
  //   8000 10000000 4*0 10000 10000000 4*0 20000 10000000 4*0 40000 10000000 4*0 80000 10000000 4*0 100000
  //   10000000 4*0 200000 10000000 4*0 400000 10000000 4*0 800000 10000000 4*0 1000000 10000000 4*0 40
  //   8000000 4*0 80 8000000 4*0 100 8000000 4*0 200 8000000 4*0 400 8000000 4*0 800 8000000 4*0 1000
  //   8000000 4*0 2000 8000000 4*0 4000 8000000 4*0 8000 8000000 4*0 10000 8000000 4*0 20000 8000000 4*0
  //   40000 8000000 4*0 80000 8000000 4*0 100000 8000000 4*0 200000 8000000 4*0 400000 8000000 4*0 800000
  //   8000000 4*0 1000000 8000000 4*0 2000000 8000000 4*0 20 4000000 4*0 40 4000000 4*0 80 4000000 4*0 100
  //   4000000 4*0 200 4000000 4*0 400 4000000 4*0 800 4000000 4*0 1000 4000000 4*0 2000 4000000 4*0 4000
  //   4000000 4*0 8000 4000000 4*0 10000 4000000 4*0 20000 4000000 4*0 40000 4000000 4*0 80000 4000000 4*0
  //   100000 4000000 4*0 200000 4000000 4*0 400000 4000000 4*0 800000 4000000 4*0 1000000 4000000 4*0
  //   2000000 4000000 4*0 4000000 4000000 4*0 10 2000000 4*0 20 2000000 4*0 40 2000000 4*0 80 2000000 4*0
  //   100 2000000 4*0 200 2000000 4*0 400 2000000 4*0 800 2000000 4*0 1000 2000000 4*0 2000 2000000 4*0
  //   4000 2000000 4*0 8000 2000000 4*0 10000 2000000 4*0 20000 2000000 4*0 40000 2000000 4*0 80000
  //   2000000 4*0 100000 2000000 4*0 200000 2000000 4*0 400000 2000000 4*0 800000 2000000 4*0 1000000
  //   2000000 4*0 2000000 2000000 4*0 4000000 2000000 4*0 10 1000000 4*0 20 1000000 4*0 40 1000000 4*0 80
  //   1000000 4*0 100 1000000 4*0 200 1000000 4*0 400 1000000 4*0 800 1000000 4*0 1000 1000000 4*0 2000
  //   1000000 4*0 4000 1000000 4*0 8000 1000000 4*0 10000 1000000 4*0 20000 1000000 4*0 40000 1000000 4*0
  //   80000 1000000 4*0 100000 1000000 4*0 200000 1000000 4*0 400000 1000000 4*0 800000 1000000 4*0
  //   1000000 1000000 4*0 2000000 1000000 4*0 4000000 1000000 4*0 8000000 1000000 4*0 8 800000 4*0 10
  //   800000 4*0 20 800000 4*0 40 800000 4*0 80 800000 4*0 100 800000 4*0 200 800000 4*0 400 800000 4*0
  //   800 800000 4*0 1000 800000 4*0 2000 800000 4*0 4000 800000 4*0 8000 800000 4*0 10000 800000 4*0
  //   20000 800000 4*0 40000 800000 4*0 80000 800000 4*0 100000 800000 4*0 200000 800000 4*0 400000 800000
  //   4*0 800000 800000 4*0 1000000 800000 4*0 2000000 800000 4*0 4000000 800000 4*0 8000000 800000 4*0 8
  //   400000 4*0 10 400000 4*0 20 400000 4*0 40 400000 4*0 80 400000 4*0 100 400000 4*0 200 400000 4*0 400
  //   400000 4*0 800 400000 4*0 1000 400000 4*0 2000 400000 4*0 4000 400000 4*0 8000 400000 4*0 10000
  //   400000 4*0 20000 400000 4*0 40000 400000 4*0 80000 400000 4*0 100000 400000 4*0 200000 400000 4*0
  //   400000 400000 4*0 800000 400000 4*0 1000000 400000 4*0 2000000 400000 4*0 8 200000 4*0 10 200000 4*0
  //   20 200000 4*0 40 200000 4*0 80 200000 4*0 100 200000 4*0 200 200000 4*0 400 200000 4*0 800 200000
  //   4*0 1000 200000 4*0 2000 200000 4*0 4000 200000 4*0 8000 200000 4*0 10000 200000 4*0 20000 200000
  //   4*0 40000 200000 4*0 80000 200000 4*0 100000 200000 4*0 200000 200000 4*0 400000 200000 4*0 800000
  //   200000 4*0 8 100000 4*0 10 100000 4*0 20 100000 4*0 40 100000 4*0 80 100000 4*0 100 100000 4*0 200
  //   100000 4*0 400 100000 4*0 800 100000 4*0 1000 100000 4*0 2000 100000 4*0 4000 100000 4*0 8000 100000
  //   4*0 10000 100000 4*0 20000 100000 4*0 40000 100000 4*0 80000 100000 4*0 100000 100000 4*0 200000
  //   100000 4*0 8 80000 4*0 10 80000 4*0 20 80000 4*0 40 80000 4*0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
  //   Loading
  //   contents of rom_2 (hex, n*v repeats v):
  //   8 200000 20 4000 10 2000 20 2000 40 2000 20 1000 2000 800 4000 800 8000 800 2000 400 4000 400 8000
  //   400 2000 200 4000 200 8000 200 4066*0 1000000 8000 2000000 8000 4000000 8000 1000000 4000 2000000
  //   4000 4000000 4000 20 2000 1000000 2000 2000000 2000 4000000 2000 4000 800 2000 400 4000 400 8000 400
  //   4000 200 4066*0 8000000 200000 10000000 200000 20000000 200000 8000000 100000 10000000 100000
  //   20000000 100000 8000000 80000 10000000 80000 20000000 80000 2000000 8000 1000000 4000 2000000 4000
  //   4000000 4000 2000000 2000 8000 400 4066*0 2000000 20000000 4000000 20000000 8000000 20000000 2000000
  //   10000000 4000000 10000000 8000000 10000000 2000000 8000000 4000000 8000000 8000000 8000000 10000000
  //   200000 8000000 100000 10000000 100000 20000000 100000 10000000 80000 2000000 4000 4066*0 10000
  //   80000000 20000 80000000 40000 80000000 10000 40000000 20000 40000000 40000 40000000 10000 20000000
  //   20000 20000000 40000 20000000 4000000 20000000 2000000 10000000 4000000 10000000 8000000 10000000
  //   4000000 8000000 10000000 100000 4066*0 20000 80000000 10 40000000 20 40000000 40 40000000 10000
  //   40000000 20000 40000000 40000 40000000 10 20000000 20 20000000 40 20000000 20000 20000000 10
  //   10000000 20 10000000 40 10000000 4000000 10000000 4066*0 20 40000000 20000 40000000 10 20000000 20
  //   20000000 40 20000000 20 10000000 4 400000 8 400000 10 400000 4 200000 8 200000 10 200000 4 100000 8
  //   100000 10 100000 4066*0 20 20000000 8 400000 4 200000 8 200000 10 200000 8 100000 10 4000 20 4000 40
  //   4000 10 2000 20 2000 40 2000 10 1000 20 1000 40 1000
endmodule

module HexDisplaySplitter (
  input  [22:0] In,
  output [3:0] Out_0,
  output [3:0] Out_1,
  output [3:0] Out_2,
  output [3:0] Out_3,
  output [3:0] Out_4,
  output [3:0] Out_5
);


  assign Out_0 = In[3:0];
  assign Out_1 = In[7:4];
  assign Out_2 = In[11:8];
  assign Out_3 = In[15:12];
  assign Out_4 = In[19:16];
  assign Out_5 = {1'b0, In[22:20]};
endmodule
